// Logisim project CMOS.circ as structural Verilog: 1 circuit, main circuit main
module main (
  input  in_1,
  input  in_2,
  input  in_3,
  input  in_4,
  input  in_5,
  input  in_6,
  input  in_7,
  input  in_8,
  input  in_9,
  output out_10,
  output out_11,
  output out_12,
  output out_13,
  output out_14
);

  wire transistor_3_out, transistor_4_out, transistor_10_out, transistor_13_out, transistor_16_out,
       transistor_19_out;

  Transistor transistor_1 (.in(1'b1), .out(out_10), .gate(in_5));
  Transistor #(.\type ("n")) transistor_2 (.in(1'b0), .out(out_10), .gate(in_5));
  Transistor #(.\type ("n")) transistor_3 (.in(1'b0), .out(transistor_3_out), .gate(in_6));
  Transistor transistor_4 (.in(1'b1), .out(transistor_4_out), .gate(in_6));
  Transistor transistor_5 (.in(transistor_4_out), .out(transistor_3_out), .gate(in_9));
  Transistor #(.\type ("n")) transistor_6 (.in(1'b0), .out(transistor_3_out), .gate(in_9));
  Transistor #(.\type ("n")) transistor_7 (.in(1'b0), .out(out_11), .gate(in_1));
  Transistor transistor_8 (.in(1'b1), .out(out_13), .gate(transistor_3_out));
  Transistor #(.\type ("n")) transistor_9 (.in(1'b0), .out(out_13), .gate(transistor_3_out));
  Transistor transistor_10 (.in(1'b1), .out(transistor_10_out), .gate(in_1));
  Transistor transistor_11 (.in(transistor_10_out), .out(out_11), .gate(in_4));
  Transistor #(.\type ("n")) transistor_12 (.in(1'b0), .out(out_11), .gate(in_4));
  Transistor transistor_13 (.in(1'b1), .out(transistor_13_out), .gate(in_7));
  Transistor transistor_14 (.in(1'b1), .out(transistor_13_out), .gate(in_8));
  Transistor #(.\type ("n")) transistor_15 (.in(transistor_16_out), .out(transistor_13_out), .gate(in_7));
  Transistor #(.\type ("n")) transistor_16 (.in(1'b0), .out(transistor_16_out), .gate(in_8));
  Transistor transistor_17 (.in(1'b1), .out(out_12), .gate(in_2));
  Transistor #(.\type ("n")) transistor_18 (.in(transistor_19_out), .out(out_12), .gate(in_2));
  Transistor #(.\type ("n")) transistor_19 (.in(1'b0), .out(transistor_19_out), .gate(in_3));
  Transistor transistor_20 (.in(1'b1), .out(out_14), .gate(transistor_13_out));
  Transistor #(.\type ("n")) transistor_21 (.in(1'b0), .out(out_14), .gate(transistor_13_out));
  Transistor transistor_22 (.in(1'b1), .out(out_12), .gate(in_3));

  // Notes on the sheet:
  //   NOT Gate
  //   OR Gate
  //   NOR Gate
  //   AND Gate
  //   NAND Gate
endmodule
