// Logisim project NMos.circ as structural Verilog: 7 circuits, main circuit main
module main (
  input  in_1,
  input  in_2,
  input  in_3,
  input  in_4,
  input  in_5,
  input  in_6,
  input  in_7,
  input  in_8,
  input  in_9,
  output out_10,
  output out_11,
  output out_12,
  output out_13,
  output out_14
);

  wire pull_resistor_2_node, pull_resistor_5_node, transistor_3_out, transistor_6_out;

  Pull_Resistor #(.pull(1)) pull_resistor_1 (.node(out_10));
  Transistor #(.\type ("n")) transistor_1 (.in(1'b0), .out(out_10), .gate(in_3));
  Pull_Resistor #(.pull(1)) pull_resistor_2 (.node(pull_resistor_2_node));
  Transistor #(.\type ("n")) transistor_2 (.in(transistor_3_out), .out(pull_resistor_2_node), .gate(in_6));
  Transistor #(.\type ("n")) transistor_3 (.in(1'b0), .out(transistor_3_out), .gate(in_8));
  Pull_Resistor #(.pull(1)) pull_resistor_3 (.node(out_13));
  Transistor #(.\type ("n")) transistor_4 (.in(1'b0), .out(out_13), .gate(pull_resistor_2_node));
  Pull_Resistor #(.pull(1)) pull_resistor_4 (.node(out_11));
  Transistor #(.\type ("n")) transistor_5 (.in(transistor_6_out), .out(out_11), .gate(in_1));
  Transistor #(.\type ("n")) transistor_6 (.in(1'b0), .out(transistor_6_out), .gate(in_4));
  Pull_Resistor #(.pull(1)) pull_resistor_5 (.node(pull_resistor_5_node));
  Transistor #(.\type ("n")) transistor_7 (.in(1'b0), .out(pull_resistor_5_node), .gate(in_7));
  Transistor #(.\type ("n")) transistor_8 (.in(1'b0), .out(pull_resistor_5_node), .gate(in_9));
  Pull_Resistor #(.pull(1)) pull_resistor_6 (.node(out_14));
  Transistor #(.\type ("n")) transistor_9 (.in(1'b0), .out(out_14), .gate(pull_resistor_5_node));
  Pull_Resistor #(.pull(1)) pull_resistor_7 (.node(out_12));
  Transistor #(.\type ("n")) transistor_10 (.in(1'b0), .out(out_12), .gate(in_2));
  Transistor #(.\type ("n")) transistor_11 (.in(1'b0), .out(out_12), .gate(in_5));

  // Notes on the sheet:
  //   NOT Gate
  //   AND Gate
  //   NAND Gate
  //   OR Gate
  //   NOR Gate
endmodule

module Adder1Bit (
  input  A,
  input  B,
  input  Cin,
  output S,
  output Co
);

  wire and_1_out, and_2_out, xor_1_out;

  and and_1 (and_1_out, B, A);
  xor xor_1 (xor_1_out, A, B);
  xor xor_2 (S, xor_1_out, Cin);
  and and_2 (and_2_out, Cin, xor_1_out);
  or or_1 (Co, and_1_out, and_2_out);

  // Notes on the sheet:
  //   1 Bit Full Adder
endmodule

module Adder4Bit (
  input  [3:0] A,
  input  [3:0] B,
  input  Cin,
  output Co,
  output [3:0] S
);

  wire adder1bit_2_co, adder1bit_3_co, adder1bit_4_co;

  Adder1Bit adder1bit_1 (.A(A[3]), .B(B[3]), .Cin(adder1bit_2_co), .S(S[3]), .Co(Co));
  Adder1Bit adder1bit_2 (.A(A[2]), .B(B[2]), .Cin(adder1bit_3_co), .S(S[2]), .Co(adder1bit_2_co));
  Adder1Bit adder1bit_3 (.A(A[1]), .B(B[1]), .Cin(adder1bit_4_co), .S(S[1]), .Co(adder1bit_3_co));
  Adder1Bit adder1bit_4 (.A(A[0]), .B(B[0]), .Cin(Cin), .S(S[0]), .Co(adder1bit_4_co));
endmodule

module Adder4BitBlock (
  input  [3:0] in_1,
  input  in_2,
  input  [3:0] in_3,
  output out_4,
  output [3:0] out_5
);

  main main_1 ();  // open: in_1, in_2, in_3, in_4, in_5, in_6, in_7, in_8, in_9, out_10, out_11, out_12, out_13, out_14
  Adder4Bit adder4bit_1 (.Cin(in_2), .A(in_1), .B(in_3), .S(out_5), .Co(out_4));
endmodule

module AddSub (
  input  [3:0] A,
  input  [3:0] B,
  input  Op,
  output out_4,
  output [3:0] S
);

  wire adder1bit_2_co, adder1bit_3_co, adder1bit_4_co, xor_1_out, xor_2_out, xor_3_out, xor_4_out;

  xor xor_1 (xor_1_out, B[3], Op);
  Adder1Bit adder1bit_1 (.A(A[3]), .B(xor_1_out), .Cin(adder1bit_2_co), .S(S[3]), .Co(out_4));
  xor xor_2 (xor_2_out, B[2], Op);
  Adder1Bit adder1bit_2 (.A(A[2]), .B(xor_2_out), .Cin(adder1bit_3_co), .S(S[2]), .Co(adder1bit_2_co));
  xor xor_3 (xor_3_out, B[1], Op);
  Adder1Bit adder1bit_3 (.A(A[1]), .B(xor_3_out), .Cin(adder1bit_4_co), .S(S[1]), .Co(adder1bit_3_co));
  xor xor_4 (xor_4_out, B[0], Op);
  Adder1Bit adder1bit_4 (.A(A[0]), .B(xor_4_out), .Cin(Op), .S(S[0]), .Co(adder1bit_4_co));

  // Notes on the sheet:
  //   else it will work as 4 bit subtractor
  //   if(op == 0) it will works as 4 bit adder
  //   4 Bit Signed Subtraction.
endmodule

module Subtraction1 (
  input  A,
  input  B,
  input  Bin,
  output D,
  output Bo
);

  wire and_1_out, and_2_out, not_1_out, not_2_out, xor_1_out;

  not not_1 (not_1_out, A);
  xor xor_1 (xor_1_out, A, B);
  and and_1 (and_1_out, B, not_1_out);
  not not_2 (not_2_out, xor_1_out);
  xor xor_2 (D, xor_1_out, Bin);
  and and_2 (and_2_out, Bin, not_2_out);
  or or_1 (Bo, and_2_out, and_1_out);

  // Notes on the sheet:
  //   1 Bit Unsigned Subtraction
  //   D = A - B
endmodule

module Subtraction4 (
  input  [3:0] in_1,
  input  [3:0] in_2,
  input  in_3,
  output out_4,
  output [3:0] out_5
);

  wire subtraction1_2_bo, subtraction1_3_bo, subtraction1_4_bo;

  Subtraction1 subtraction1_1 (.A(in_1[3]), .B(in_2[3]), .Bin(subtraction1_2_bo), .D(out_5[3]), .Bo(out_4));
  Subtraction1 subtraction1_2 (.A(in_1[2]), .B(in_2[2]), .Bin(subtraction1_3_bo), .D(out_5[2]), .Bo(subtraction1_2_bo));
  Subtraction1 subtraction1_3 (.A(in_1[1]), .B(in_2[1]), .Bin(subtraction1_4_bo), .D(out_5[1]), .Bo(subtraction1_3_bo));
  Subtraction1 subtraction1_4 (.A(in_1[0]), .B(in_2[0]), .Bin(in_3), .D(out_5[0]), .Bo(subtraction1_4_bo));

  // Notes on the sheet:
  //   4 Bit Unsigned Subtraction
endmodule
