// Logisim project Resistor.circ as structural Verilog: 6 circuits, main circuit RF1Bit
module RF1Bit (
  input  Din,
  input  Sel,
  input  CLK,
  output Dout
);

  wire multiplexer_1_out;

  Multiplexer multiplexer_1 (.in0(Dout), .in1(Din), .out(multiplexer_1_out), .sel(Sel));
  D_Flip_Flop d_ff_1 (.D(multiplexer_1_out), .clk(CLK), .Q(Dout));  // open: Qn, preset, reset
endmodule

module RF2bit (
  input  [1:0] Din,
  input  Sel,
  input  CLK,
  output [1:0] Dout
);

  RF1Bit rf1bit_1 (.Din(Din[0]), .Sel(Sel), .CLK(CLK), .Dout(Dout[0]));
  RF1Bit rf1bit_2 (.Din(Din[1]), .Sel(Sel), .CLK(CLK), .Dout(Dout[1]));
endmodule

module RF_Set (
  input  [1:0] WRD,
  input  RE,
  input  [1:0] WR,
  input  CLK,
  input  [1:0] RA,
  input  [1:0] RB,
  output [1:0] A,
  output [1:0] B
);

  wire decoder_1_out0, decoder_1_out1, decoder_1_out2, decoder_1_out3;
  wire [1:0] rf2bit_1_dout, rf2bit_2_dout, rf2bit_3_dout, rf2bit_4_dout;

  Decoder #(.select(2)) decoder_1 (
    .out0(decoder_1_out0), .out1(decoder_1_out1), .out2(decoder_1_out2), .out3(decoder_1_out3), .sel(WR),
    .en(RE));
  RF2bit rf2bit_1 (.Sel(decoder_1_out0), .CLK(CLK), .Din(WRD), .Dout(rf2bit_1_dout));
  RF2bit rf2bit_2 (.Sel(decoder_1_out1), .CLK(CLK), .Din(WRD), .Dout(rf2bit_2_dout));
  RF2bit rf2bit_3 (.Sel(decoder_1_out2), .CLK(CLK), .Din(WRD), .Dout(rf2bit_3_dout));
  RF2bit rf2bit_4 (.Sel(decoder_1_out3), .CLK(CLK), .Din(WRD), .Dout(rf2bit_4_dout));
  Multiplexer #(.select(2), .width(2)) multiplexer_1 (
    .in0(rf2bit_1_dout), .in1(rf2bit_2_dout), .in2(rf2bit_3_dout), .in3(rf2bit_4_dout), .out(A), .sel(RA));
  Multiplexer #(.select(2), .width(2)) multiplexer_2 (
    .in0(rf2bit_1_dout), .in1(rf2bit_2_dout), .in2(rf2bit_3_dout), .in3(rf2bit_4_dout), .out(B), .sel(RB));
endmodule

module RAM1X1 (
  input  RS1,
  input  WD,
  input  WS,
  input  RS2,
  input  CLK,
  output RD1,
  output RD2
);

  wire d_ff_1_q, multiplexer_1_out;

  Multiplexer multiplexer_1 (.in0(d_ff_1_q), .in1(WD), .out(multiplexer_1_out), .sel(WS));
  D_Flip_Flop d_ff_1 (.D(multiplexer_1_out), .clk(CLK), .Q(d_ff_1_q));  // open: Qn, preset, reset
  and and_1 (RD1, RS1, d_ff_1_q);
  and and_2 (RD2, d_ff_1_q, RS2);
endmodule

module RAM1X2 (
  input  [1:0] WD,
  input  RS1,
  input  RS2,
  input  WS,
  input  CLK,
  output [1:0] RD1,
  output [1:0] RD2
);

  RAM1X1 ram1x1_1 (.WD(WD[1]), .WS(WS), .CLK(CLK), .RS1(RS1), .RS2(RS2), .RD1(RD1[1]), .RD2(RD2[1]));
  RAM1X1 ram1x1_2 (.WD(WD[0]), .WS(WS), .CLK(CLK), .RS1(RS1), .RS2(RS2), .RD1(RD1[0]), .RD2(RD2[0]));

  // Other names for the same wires on the sheet: R10 = RD1[0]; R11 = RD1[1]; R20 = RD2[0]; R21 = RD2[1]; W0 = WD[0];
  //   W1 = WD[1]
endmodule

module RAM2X2 (
  input  [1:0] WD
);

  RAM1X2 ram1x2_1 (.WD(WD));  // open: RS1, RS2, WS, CLK, RD2, RD1
  RAM1X2 ram1x2_2 (.WD(WD));  // open: RS1, RS2, WS, CLK, RD2, RD1
endmodule
