// Logisim project Singed_Multiplier.circ as structural Verilog: 5 circuits, main circuit main
module main (
  input  a,
  input  b,
  input  H,
  input  Ci,
  input  D,
  output Z,
  output Co,
  output H_c,
  output D_c,
  output b_c
);

  wire and_1_out, and_2_out, and_3_out, and_4_out, or_1_out, xor_1_out, xor_2_out;

  and and_1 (and_1_out, b, H);
  and and_2 (and_2_out, H, Ci);
  and and_3 (and_3_out, Ci, b);
  or or_1 (or_1_out, Ci, b);
  xor xor_1 (xor_1_out, a, D);
  and and_4 (and_4_out, or_1_out, xor_1_out);
  xor xor_2 (xor_2_out, a, and_1_out);
  or or_2 (Co, and_3_out, and_4_out);
  xor xor_3 (Z, xor_2_out, and_2_out);

  assign b_c = b;
  assign D_c = D;
  assign H_c = H;

  // Notes on the sheet:
  //   Booth Multiplier Building Block (Cell B)
endmodule

module CellC (
  input  x_i_1,
  input  x_i,
  output H,
  output D
);

  wire not_1_out;

  not not_1 (not_1_out, x_i_1);
  xor xor_1 (H, x_i_1, x_i);
  and and_1 (D, x_i, not_1_out);

  // Notes on the sheet:
  //   Booth Multiplier Building Block (Cell C)
endmodule

module Multiplier2 (
  input  y1,
  input  y0,
  input  x0,
  input  x1,
  output out_5,
  output out_6,
  output out_7,
  output out_8
);

  wire cellc_1_d, cellc_1_h, cellc_2_d, cellc_2_h, main_1_z, main_3_b_c, main_3_co, main_3_d_c, main_3_h_c,
       main_3_z, main_4_co, main_4_d_c, main_4_h_c, main_5_b_c, main_5_co, main_5_d_c, main_5_h_c, main_5_z,
       main_6_co, main_6_d_c, main_6_h_c, main_7_b_c, main_7_co, main_7_d_c, main_7_h_c;

  main main_1 (
    .a(1'b0), .b(y1), .H(main_3_h_c), .Ci(main_3_co), .D(main_3_d_c), .Z(main_1_z));  // open: Co, H_c, D_c, b_c
  main main_2 (
    .a(main_1_z), .b(main_3_b_c), .H(main_4_h_c), .Ci(main_4_co), .D(main_4_d_c), .Z(out_5));  // open: Co, H_c, D_c, b_c
  main main_3 (
    .a(1'b0), .b(y1), .H(main_5_h_c), .Ci(main_5_co), .D(main_5_d_c), .Co(main_3_co), .H_c(main_3_h_c),
    .D_c(main_3_d_c), .b_c(main_3_b_c), .Z(main_3_z));
  main main_4 (
    .a(main_3_z), .b(main_5_b_c), .H(main_6_h_c), .Ci(main_6_co), .D(main_6_d_c), .Co(main_4_co),
    .H_c(main_4_h_c), .D_c(main_4_d_c), .Z(out_6));  // open: b_c
  main main_5 (
    .a(1'b0), .b(y1), .H(main_7_h_c), .Ci(main_7_co), .D(main_7_d_c), .Co(main_5_co), .H_c(main_5_h_c),
    .D_c(main_5_d_c), .b_c(main_5_b_c), .Z(main_5_z));
  main main_6 (
    .a(main_5_z), .b(main_7_b_c), .H(cellc_2_h), .Ci(1'b0), .D(cellc_2_d), .Co(main_6_co), .H_c(main_6_h_c),
    .D_c(main_6_d_c), .Z(out_7));  // open: b_c
  main main_7 (
    .a(1'b0), .b(y0), .H(cellc_1_h), .Ci(1'b0), .D(cellc_1_d), .Co(main_7_co), .H_c(main_7_h_c),
    .D_c(main_7_d_c), .b_c(main_7_b_c), .Z(out_8));
  CellC cellc_1 (.x_i_1(1'b0), .x_i(x0), .H(cellc_1_h), .D(cellc_1_d));
  CellC cellc_2 (.x_i_1(x0), .x_i(x1), .H(cellc_2_h), .D(cellc_2_d));
endmodule

module Multiplier3 (
  input  in_1,
  input  in_2,
  input  in_3,
  input  in_4,
  input  in_5,
  input  in_6,
  input  in_7,
  output out_8,
  output out_9,
  output out_10,
  output out_11,
  output out_12,
  output out_13
);

  wire cellc_1_d, cellc_1_h, cellc_2_d, cellc_2_h, cellc_3_d, cellc_3_h, cellc_4_h, main_1_z, main_2_z,
       main_3_z, main_5_b_c, main_5_co, main_5_d_c, main_5_h_c, main_5_z, main_6_b_c, main_6_co, main_6_d_c,
       main_6_h_c, main_6_z, main_7_b_c, main_7_co, main_7_d_c, main_7_h_c, main_7_z, main_8_co, main_8_d_c,
       main_8_h_c, main_9_b_c, main_9_co, main_9_d_c, main_9_h_c, main_9_z, main_10_b_c, main_10_co,
       main_10_d_c, main_10_h_c, main_10_z, main_11_b_c, main_11_co, main_11_d_c, main_11_h_c, main_11_z,
       main_12_co, main_12_d_c, main_12_h_c, main_13_b_c, main_13_co, main_13_d_c, main_13_h_c, main_13_z,
       main_14_b_c, main_14_co, main_14_d_c, main_14_h_c, main_14_z, main_15_b_c, main_15_co, main_15_d_c,
       main_15_h_c, main_16_b_c, main_16_co, main_16_d_c, main_16_h_c, main_16_z, main_17_b_c, main_17_co,
       main_17_d_c, main_17_h_c, main_18_b_c, main_18_co, main_18_d_c, main_18_h_c;

  main main_1 (
    .a(1'b0), .b(in_1), .H(main_5_h_c), .Ci(main_5_co), .D(main_5_d_c), .Z(main_1_z));  // open: Co, H_c, D_c, b_c
  main main_2 (
    .a(main_1_z), .b(main_5_b_c), .H(main_6_h_c), .Ci(main_6_co), .D(main_6_d_c), .Z(main_2_z));  // open: Co, H_c, D_c, b_c
  main main_3 (
    .a(main_2_z), .b(main_6_b_c), .H(main_7_h_c), .Ci(main_7_co), .D(main_7_d_c), .Z(main_3_z));  // open: Co, H_c, D_c, b_c
  main main_4 (
    .a(main_3_z), .b(main_7_b_c), .H(main_8_h_c), .Ci(main_8_co), .D(main_8_d_c), .Z(out_8));  // open: Co, H_c, D_c, b_c
  main main_5 (
    .a(1'b0), .b(in_1), .H(main_9_h_c), .Ci(main_9_co), .D(main_9_d_c), .Co(main_5_co), .H_c(main_5_h_c),
    .D_c(main_5_d_c), .b_c(main_5_b_c), .Z(main_5_z));
  main main_6 (
    .a(main_5_z), .b(main_9_b_c), .H(main_10_h_c), .Ci(main_10_co), .D(main_10_d_c), .Co(main_6_co),
    .H_c(main_6_h_c), .D_c(main_6_d_c), .b_c(main_6_b_c), .Z(main_6_z));
  main main_7 (
    .a(main_6_z), .b(main_10_b_c), .H(main_11_h_c), .Ci(main_11_co), .D(main_11_d_c), .Co(main_7_co),
    .H_c(main_7_h_c), .D_c(main_7_d_c), .b_c(main_7_b_c), .Z(main_7_z));
  main main_8 (
    .a(main_7_z), .b(main_11_b_c), .H(main_12_h_c), .Ci(main_12_co), .D(main_12_d_c), .Co(main_8_co),
    .H_c(main_8_h_c), .D_c(main_8_d_c), .Z(out_9));  // open: b_c
  main main_9 (
    .a(1'b0), .b(in_1), .H(main_13_h_c), .Ci(main_13_co), .D(main_13_d_c), .Co(main_9_co), .H_c(main_9_h_c),
    .D_c(main_9_d_c), .b_c(main_9_b_c), .Z(main_9_z));
  main main_10 (
    .a(main_9_z), .b(main_13_b_c), .H(main_14_h_c), .Ci(main_14_co), .D(main_14_d_c), .Co(main_10_co),
    .H_c(main_10_h_c), .D_c(main_10_d_c), .b_c(main_10_b_c), .Z(main_10_z));
  main main_11 (
    .a(main_10_z), .b(main_14_b_c), .H(main_15_h_c), .Ci(main_15_co), .D(main_15_d_c), .Co(main_11_co),
    .H_c(main_11_h_c), .D_c(main_11_d_c), .b_c(main_11_b_c), .Z(main_11_z));
  main main_12 (
    .a(main_11_z), .b(main_15_b_c), .H(cellc_4_h), .Ci(1'b0), .D(out_11), .Co(main_12_co), .H_c(main_12_h_c),
    .D_c(main_12_d_c), .Z(out_10));  // open: b_c
  main main_13 (
    .a(1'b0), .b(in_1), .H(main_16_h_c), .Ci(main_16_co), .D(main_16_d_c), .Co(main_13_co),
    .H_c(main_13_h_c), .D_c(main_13_d_c), .b_c(main_13_b_c), .Z(main_13_z));
  main main_14 (
    .a(main_13_z), .b(main_16_b_c), .H(main_17_h_c), .Ci(main_17_co), .D(main_17_d_c), .Co(main_14_co),
    .H_c(main_14_h_c), .D_c(main_14_d_c), .b_c(main_14_b_c), .Z(main_14_z));
  main main_15 (
    .a(main_14_z), .b(main_17_b_c), .H(cellc_3_h), .Ci(1'b0), .D(cellc_3_d), .Co(main_15_co),
    .H_c(main_15_h_c), .D_c(main_15_d_c), .b_c(main_15_b_c), .Z(out_11));
  main main_16 (
    .a(1'b0), .b(in_2), .H(main_18_h_c), .Ci(main_18_co), .D(main_18_d_c), .Co(main_16_co),
    .H_c(main_16_h_c), .D_c(main_16_d_c), .b_c(main_16_b_c), .Z(main_16_z));
  main main_17 (
    .a(main_16_z), .b(main_18_b_c), .H(cellc_2_h), .Ci(1'b0), .D(cellc_2_d), .Co(main_17_co),
    .H_c(main_17_h_c), .D_c(main_17_d_c), .b_c(main_17_b_c), .Z(out_12));
  main main_18 (
    .a(1'b0), .b(in_3), .H(cellc_1_h), .Ci(1'b0), .D(cellc_1_d), .Co(main_18_co), .H_c(main_18_h_c),
    .D_c(main_18_d_c), .b_c(main_18_b_c), .Z(out_13));
  CellC cellc_1 (.x_i_1(1'b0), .x_i(in_4), .H(cellc_1_h), .D(cellc_1_d));
  CellC cellc_2 (.x_i_1(in_4), .x_i(in_5), .H(cellc_2_h), .D(cellc_2_d));
  CellC cellc_3 (.x_i_1(in_5), .x_i(in_6), .H(cellc_3_h), .D(cellc_3_d));
  CellC cellc_4 (.x_i_1(in_6), .x_i(in_7), .H(cellc_4_h), .D(out_11));
endmodule

module Multiplier4 (
  input  in_1,
  input  in_2,
  input  in_3,
  input  in_4,
  input  in_5,
  input  in_6,
  input  in_7,
  input  in_8,
  output out_9,
  output out_10,
  output out_11,
  output out_12,
  output out_13,
  output out_14,
  output out_15,
  output out_16
);

  wire cellc_1_d, cellc_1_h, cellc_2_d, cellc_2_h, cellc_3_d, cellc_3_h, cellc_4_d, cellc_4_h, main_1_z,
       main_2_z, main_3_z, main_5_b_c, main_5_co, main_5_d_c, main_5_h_c, main_5_z, main_6_b_c, main_6_co,
       main_6_d_c, main_6_h_c, main_6_z, main_7_b_c, main_7_co, main_7_d_c, main_7_h_c, main_7_z, main_8_co,
       main_8_d_c, main_8_h_c, main_9_b_c, main_9_co, main_9_d_c, main_9_h_c, main_9_z, main_10_b_c,
       main_10_co, main_10_d_c, main_10_h_c, main_10_z, main_11_b_c, main_11_co, main_11_d_c, main_11_h_c,
       main_11_z, main_12_co, main_12_d_c, main_12_h_c, main_13_b_c, main_13_co, main_13_d_c, main_13_h_c,
       main_13_z, main_14_b_c, main_14_co, main_14_d_c, main_14_h_c, main_14_z, main_15_b_c, main_15_co,
       main_15_d_c, main_15_h_c, main_15_z, main_16_co, main_16_d_c, main_16_h_c, main_17_b_c, main_17_co,
       main_17_d_c, main_17_h_c, main_17_z, main_18_b_c, main_18_co, main_18_d_c, main_18_h_c, main_18_z,
       main_19_b_c, main_19_co, main_19_d_c, main_19_h_c, main_19_z, main_20_co, main_20_d_c, main_20_h_c,
       main_21_b_c, main_21_co, main_21_d_c, main_21_h_c, main_21_z, main_22_b_c, main_22_co, main_22_d_c,
       main_22_h_c, main_22_z, main_23_b_c, main_23_co, main_23_d_c, main_23_h_c, main_24_b_c, main_24_co,
       main_24_d_c, main_24_h_c, main_24_z, main_25_b_c, main_25_co, main_25_d_c, main_25_h_c, main_26_b_c,
       main_26_co, main_26_d_c, main_26_h_c;

  main main_1 (
    .a(1'b0), .b(in_1), .H(main_5_h_c), .Ci(main_5_co), .D(main_5_d_c), .Z(main_1_z));  // open: Co, H_c, D_c, b_c
  main main_2 (
    .a(main_1_z), .b(main_5_b_c), .H(main_6_h_c), .Ci(main_6_co), .D(main_6_d_c), .Z(main_2_z));  // open: Co, H_c, D_c, b_c
  main main_3 (
    .a(main_2_z), .b(main_6_b_c), .H(main_7_h_c), .Ci(main_7_co), .D(main_7_d_c), .Z(main_3_z));  // open: Co, H_c, D_c, b_c
  main main_4 (
    .a(main_3_z), .b(main_7_b_c), .H(main_8_h_c), .Ci(main_8_co), .D(main_8_d_c), .Z(out_9));  // open: Co, H_c, D_c, b_c
  main main_5 (
    .a(1'b0), .b(in_1), .H(main_9_h_c), .Ci(main_9_co), .D(main_9_d_c), .Co(main_5_co), .H_c(main_5_h_c),
    .D_c(main_5_d_c), .b_c(main_5_b_c), .Z(main_5_z));
  main main_6 (
    .a(main_5_z), .b(main_9_b_c), .H(main_10_h_c), .Ci(main_10_co), .D(main_10_d_c), .Co(main_6_co),
    .H_c(main_6_h_c), .D_c(main_6_d_c), .b_c(main_6_b_c), .Z(main_6_z));
  main main_7 (
    .a(main_6_z), .b(main_10_b_c), .H(main_11_h_c), .Ci(main_11_co), .D(main_11_d_c), .Co(main_7_co),
    .H_c(main_7_h_c), .D_c(main_7_d_c), .b_c(main_7_b_c), .Z(main_7_z));
  main main_8 (
    .a(main_7_z), .b(main_11_b_c), .H(main_12_h_c), .Ci(main_12_co), .D(main_12_d_c), .Co(main_8_co),
    .H_c(main_8_h_c), .D_c(main_8_d_c), .Z(out_10));  // open: b_c
  main main_9 (
    .a(1'b0), .b(in_1), .H(main_13_h_c), .Ci(main_13_co), .D(main_13_d_c), .Co(main_9_co), .H_c(main_9_h_c),
    .D_c(main_9_d_c), .b_c(main_9_b_c), .Z(main_9_z));
  main main_10 (
    .a(main_9_z), .b(main_13_b_c), .H(main_14_h_c), .Ci(main_14_co), .D(main_14_d_c), .Co(main_10_co),
    .H_c(main_10_h_c), .D_c(main_10_d_c), .b_c(main_10_b_c), .Z(main_10_z));
  main main_11 (
    .a(main_10_z), .b(main_14_b_c), .H(main_15_h_c), .Ci(main_15_co), .D(main_15_d_c), .Co(main_11_co),
    .H_c(main_11_h_c), .D_c(main_11_d_c), .b_c(main_11_b_c), .Z(main_11_z));
  main main_12 (
    .a(main_11_z), .b(main_15_b_c), .H(main_16_h_c), .Ci(main_16_co), .D(main_16_d_c), .Co(main_12_co),
    .H_c(main_12_h_c), .D_c(main_12_d_c), .Z(out_13));  // open: b_c
  main main_13 (
    .a(1'b0), .b(in_1), .H(main_17_h_c), .Ci(main_17_co), .D(main_17_d_c), .Co(main_13_co),
    .H_c(main_13_h_c), .D_c(main_13_d_c), .b_c(main_13_b_c), .Z(main_13_z));
  main main_14 (
    .a(main_13_z), .b(main_17_b_c), .H(main_18_h_c), .Ci(main_18_co), .D(main_18_d_c), .Co(main_14_co),
    .H_c(main_14_h_c), .D_c(main_14_d_c), .b_c(main_14_b_c), .Z(main_14_z));
  main main_15 (
    .a(main_14_z), .b(main_18_b_c), .H(main_19_h_c), .Ci(main_19_co), .D(main_19_d_c), .Co(main_15_co),
    .H_c(main_15_h_c), .D_c(main_15_d_c), .b_c(main_15_b_c), .Z(main_15_z));
  main main_16 (
    .a(main_15_z), .b(main_19_b_c), .H(main_20_h_c), .Ci(main_20_co), .D(main_20_d_c), .Co(main_16_co),
    .H_c(main_16_h_c), .D_c(main_16_d_c), .Z(out_14));  // open: b_c
  main main_17 (
    .a(1'b0), .b(in_1), .H(main_21_h_c), .Ci(main_21_co), .D(main_21_d_c), .Co(main_17_co),
    .H_c(main_17_h_c), .D_c(main_17_d_c), .b_c(main_17_b_c), .Z(main_17_z));
  main main_18 (
    .a(main_17_z), .b(main_21_b_c), .H(main_22_h_c), .Ci(main_22_co), .D(main_22_d_c), .Co(main_18_co),
    .H_c(main_18_h_c), .D_c(main_18_d_c), .b_c(main_18_b_c), .Z(main_18_z));
  main main_19 (
    .a(main_18_z), .b(main_22_b_c), .H(main_23_h_c), .Ci(main_23_co), .D(main_23_d_c), .Co(main_19_co),
    .H_c(main_19_h_c), .D_c(main_19_d_c), .b_c(main_19_b_c), .Z(main_19_z));
  main main_20 (
    .a(main_19_z), .b(main_23_b_c), .H(cellc_4_h), .Ci(1'b0), .D(cellc_4_d), .Co(main_20_co),
    .H_c(main_20_h_c), .D_c(main_20_d_c), .Z(out_15));  // open: b_c
  main main_21 (
    .a(1'b0), .b(in_2), .H(main_24_h_c), .Ci(main_24_co), .D(main_24_d_c), .Co(main_21_co),
    .H_c(main_21_h_c), .D_c(main_21_d_c), .b_c(main_21_b_c), .Z(main_21_z));
  main main_22 (
    .a(main_21_z), .b(main_24_b_c), .H(main_25_h_c), .Ci(main_25_co), .D(main_25_d_c), .Co(main_22_co),
    .H_c(main_22_h_c), .D_c(main_22_d_c), .b_c(main_22_b_c), .Z(main_22_z));
  main main_23 (
    .a(main_22_z), .b(main_25_b_c), .H(cellc_3_h), .Ci(1'b0), .D(cellc_3_d), .Co(main_23_co),
    .H_c(main_23_h_c), .D_c(main_23_d_c), .b_c(main_23_b_c), .Z(out_16));
  main main_24 (
    .a(1'b0), .b(in_3), .H(main_26_h_c), .Ci(main_26_co), .D(main_26_d_c), .Co(main_24_co),
    .H_c(main_24_h_c), .D_c(main_24_d_c), .b_c(main_24_b_c), .Z(main_24_z));
  main main_25 (
    .a(main_24_z), .b(main_26_b_c), .H(cellc_2_h), .Ci(1'b0), .D(cellc_2_d), .Co(main_25_co),
    .H_c(main_25_h_c), .D_c(main_25_d_c), .b_c(main_25_b_c), .Z(out_11));
  main main_26 (
    .a(1'b0), .b(in_4), .H(cellc_1_h), .Ci(1'b0), .D(cellc_1_d), .Co(main_26_co), .H_c(main_26_h_c),
    .D_c(main_26_d_c), .b_c(main_26_b_c), .Z(out_12));
  CellC cellc_1 (.x_i_1(1'b0), .x_i(in_5), .H(cellc_1_h), .D(cellc_1_d));
  CellC cellc_2 (.x_i_1(in_5), .x_i(in_6), .H(cellc_2_h), .D(cellc_2_d));
  CellC cellc_3 (.x_i_1(in_6), .x_i(in_7), .H(cellc_3_h), .D(cellc_3_d));
  CellC cellc_4 (.x_i_1(in_7), .x_i(in_8), .H(cellc_4_h), .D(cellc_4_d));
endmodule
