// Logisim project Unsigned_Division.circ as structural Verilog: 3 circuits, main circuit main
module main (
  input  A,
  input  B,
  input  Bi,
  output S,
  output Bo
);

  wire and_1_out, and_2_out, not_1_out, not_2_out, xor_1_out;

  not not_1 (not_1_out, A);
  xor xor_1 (xor_1_out, A, B);
  and and_1 (and_1_out, B, not_1_out);
  not not_2 (not_2_out, xor_1_out);
  xor xor_2 (S, xor_1_out, Bi);
  and and_2 (and_2_out, Bi, not_2_out);
  or or_1 (Bo, and_1_out, and_2_out);

  // Notes on the sheet:
  //   1 Bit Full Subtractor
endmodule

module CellD (
  input  A,
  input  B,
  input  Bi,
  input  Sel,
  output Bo,
  output Sel_c,
  output A_D,
  output B_c
);

  wire main_1_s;

  main main_1 (.A(A), .B(B), .Bi(Bi), .S(main_1_s), .Bo(Bo));
  Multiplexer multiplexer_1 (.in0(main_1_s), .in1(A), .out(A_D), .sel(Sel));

  assign B_c = B;
  assign Sel_c = Sel;
endmodule

module Divider2 (
  input  A1,
  input  A0,
  input  B1,
  input  B0,
  output R1,
  output R0,
  output Exception,
  output Q1,
  output Q0
);

  wire celld_1_b_c, celld_1_bo, celld_1_sel_c, celld_2_a_d, celld_2_b_c, celld_2_bo, celld_3_bo,
       celld_3_sel_c, celld_4_bo;

  not not_1 (Q1, celld_1_bo);
  CellD celld_1 (
    .Sel(celld_1_bo), .A(1'b0), .B(B1), .Bi(celld_2_bo), .Bo(celld_1_bo), .B_c(celld_1_b_c),
    .Sel_c(celld_1_sel_c));  // open: A_D
  not not_2 (Q0, celld_3_bo);
  CellD celld_2 (
    .Sel(celld_1_sel_c), .A(A1), .B(B0), .Bi(1'b0), .Bo(celld_2_bo), .A_D(celld_2_a_d), .B_c(celld_2_b_c));  // open: Sel_c
  CellD celld_3 (
    .Sel(celld_3_bo), .A(celld_2_a_d), .B(celld_1_b_c), .Bi(celld_4_bo), .Bo(celld_3_bo), .A_D(R1),
    .Sel_c(celld_3_sel_c));  // open: B_c
  CellD celld_4 (
    .Sel(celld_3_sel_c), .A(A0), .B(celld_2_b_c), .Bi(1'b0), .Bo(celld_4_bo), .A_D(R0));  // open: B_c, Sel_c
  nor nor_1 (Exception, B0, B1);
endmodule
