// Logisim project Unsigned_Multiplier.circ as structural Verilog: 5 circuits, main circuit main
module main (
  input  A,
  input  B,
  input  Ci,
  output S,
  output Co
);

  wire and_1_out, and_2_out, xor_1_out;

  xor xor_1 (xor_1_out, A, B);
  and and_1 (and_1_out, B, A);
  xor xor_2 (S, xor_1_out, Ci);
  and and_2 (and_2_out, Ci, xor_1_out);
  or or_1 (Co, and_2_out, and_1_out);
endmodule

module Multiplier1 (
  input  x,
  input  y,
  input  b,
  input  ci,
  output co,
  output x_c,
  output s
);

  wire and_1_out;

  and and_1 (and_1_out, x, y);
  main main_1 (.A(b), .B(and_1_out), .Ci(ci), .S(s), .Co(co));

  assign x_c = x;

  // Notes on the sheet:
  //   1 Bit Multiplier Module
endmodule

module Mutiplier2 (
  input  x1,
  input  x0,
  input  y0,
  input  y1,
  output out_5,
  output out_6,
  output out_7,
  output out_8
);

  wire multiplier1_2_co, multiplier1_2_s, multiplier1_2_x_c, multiplier1_3_co, multiplier1_4_co;

  Multiplier1 multiplier1_1 (
    .x(multiplier1_2_x_c), .y(y1), .b(multiplier1_2_co), .ci(multiplier1_3_co), .co(out_5), .s(out_6));  // open: x_c
  Multiplier1 multiplier1_2 (
    .x(x1), .y(y0), .b(1'b0), .ci(multiplier1_4_co), .co(multiplier1_2_co), .x_c(multiplier1_2_x_c),
    .s(multiplier1_2_s));
  Multiplier1 multiplier1_3 (
    .x(y1), .y(y1), .b(multiplier1_2_s), .ci(1'b0), .co(multiplier1_3_co), .s(out_7));  // open: x_c
  Multiplier1 multiplier1_4 (.x(x0), .y(y0), .b(1'b0), .ci(1'b0), .co(multiplier1_4_co), .x_c(y1), .s(out_8));
endmodule

module Multiplier3 (
  input  in_1,
  input  in_2,
  input  in_3,
  input  in_4,
  input  in_5,
  input  in_6,
  output out_7,
  output out_8,
  output out_9,
  output out_10,
  output out_11,
  output out_12
);

  wire multiplier1_2_co, multiplier1_2_s, multiplier1_2_x_c, multiplier1_3_co, multiplier1_4_co,
       multiplier1_4_s, multiplier1_4_x_c, multiplier1_5_co, multiplier1_5_s, multiplier1_5_x_c,
       multiplier1_6_co, multiplier1_7_co, multiplier1_7_s, multiplier1_7_x_c, multiplier1_8_co,
       multiplier1_8_x_c, multiplier1_9_co, multiplier1_9_x_c;

  Multiplier1 multiplier1_1 (
    .x(multiplier1_2_x_c), .y(in_6), .b(multiplier1_2_co), .ci(multiplier1_3_co), .co(out_7), .s(out_8));  // open: x_c
  Multiplier1 multiplier1_2 (
    .x(multiplier1_4_x_c), .y(in_5), .b(multiplier1_4_co), .ci(multiplier1_5_co), .co(multiplier1_2_co),
    .x_c(multiplier1_2_x_c), .s(multiplier1_2_s));
  Multiplier1 multiplier1_3 (
    .x(multiplier1_5_x_c), .y(in_6), .b(multiplier1_2_s), .ci(multiplier1_6_co), .co(multiplier1_3_co),
    .s(out_9));  // open: x_c
  Multiplier1 multiplier1_4 (
    .x(in_1), .y(in_4), .b(1'b0), .ci(multiplier1_7_co), .co(multiplier1_4_co), .x_c(multiplier1_4_x_c),
    .s(multiplier1_4_s));
  Multiplier1 multiplier1_5 (
    .x(multiplier1_7_x_c), .y(in_5), .b(multiplier1_4_s), .ci(multiplier1_8_co), .co(multiplier1_5_co),
    .x_c(multiplier1_5_x_c), .s(multiplier1_5_s));
  Multiplier1 multiplier1_6 (
    .x(multiplier1_8_x_c), .y(in_6), .b(multiplier1_5_s), .ci(1'b0), .co(multiplier1_6_co), .s(out_10));  // open: x_c
  Multiplier1 multiplier1_7 (
    .x(in_2), .y(in_4), .b(1'b0), .ci(multiplier1_9_co), .co(multiplier1_7_co), .x_c(multiplier1_7_x_c),
    .s(multiplier1_7_s));
  Multiplier1 multiplier1_8 (
    .x(multiplier1_9_x_c), .y(in_5), .b(multiplier1_7_s), .ci(1'b0), .co(multiplier1_8_co),
    .x_c(multiplier1_8_x_c), .s(out_11));
  Multiplier1 multiplier1_9 (
    .x(in_3), .y(in_4), .b(1'b0), .ci(1'b0), .co(multiplier1_9_co), .x_c(multiplier1_9_x_c), .s(out_12));
endmodule

module Multiplier4 (
  input  x3,
  input  x2,
  input  x1,
  input  x0,
  input  in_5,
  input  in_6,
  input  in_7,
  input  in_8,
  output out_9,
  output out_10,
  output out_11,
  output out_12,
  output out_13,
  output out_14,
  output out_15,
  output out_16
);

  wire multiplier1_2_co, multiplier1_2_s, multiplier1_2_x_c, multiplier1_3_co, multiplier1_4_co,
       multiplier1_4_s, multiplier1_4_x_c, multiplier1_5_co, multiplier1_5_s, multiplier1_5_x_c,
       multiplier1_6_co, multiplier1_7_co, multiplier1_7_s, multiplier1_7_x_c, multiplier1_8_co,
       multiplier1_8_s, multiplier1_8_x_c, multiplier1_9_co, multiplier1_9_s, multiplier1_9_x_c,
       multiplier1_10_co, multiplier1_11_co, multiplier1_11_s, multiplier1_11_x_c, multiplier1_12_co,
       multiplier1_12_s, multiplier1_12_x_c, multiplier1_13_co, multiplier1_13_x_c, multiplier1_14_co,
       multiplier1_14_s, multiplier1_14_x_c, multiplier1_15_co, multiplier1_15_x_c, multiplier1_16_co,
       multiplier1_16_x_c;

  Multiplier1 multiplier1_1 (
    .x(multiplier1_2_x_c), .y(in_8), .b(multiplier1_2_co), .ci(multiplier1_3_co), .co(out_9), .s(out_10));  // open: x_c
  Multiplier1 multiplier1_2 (
    .x(multiplier1_4_x_c), .y(in_7), .b(multiplier1_4_co), .ci(multiplier1_5_co), .co(multiplier1_2_co),
    .x_c(multiplier1_2_x_c), .s(multiplier1_2_s));
  Multiplier1 multiplier1_3 (
    .x(multiplier1_5_x_c), .y(in_8), .b(multiplier1_2_s), .ci(multiplier1_6_co), .co(multiplier1_3_co),
    .s(out_11));  // open: x_c
  Multiplier1 multiplier1_4 (
    .x(multiplier1_7_x_c), .y(in_6), .b(multiplier1_7_co), .ci(multiplier1_8_co), .co(multiplier1_4_co),
    .x_c(multiplier1_4_x_c), .s(multiplier1_4_s));
  Multiplier1 multiplier1_5 (
    .x(multiplier1_8_x_c), .y(in_7), .b(multiplier1_4_s), .ci(multiplier1_9_co), .co(multiplier1_5_co),
    .x_c(multiplier1_5_x_c), .s(multiplier1_5_s));
  Multiplier1 multiplier1_6 (
    .x(multiplier1_9_x_c), .y(in_8), .b(multiplier1_5_s), .ci(multiplier1_10_co), .co(multiplier1_6_co),
    .s(out_12));  // open: x_c
  Multiplier1 multiplier1_7 (
    .x(x3), .y(in_5), .b(1'b0), .ci(multiplier1_11_co), .co(multiplier1_7_co), .x_c(multiplier1_7_x_c),
    .s(multiplier1_7_s));
  Multiplier1 multiplier1_8 (
    .x(multiplier1_11_x_c), .y(in_6), .b(multiplier1_7_s), .ci(multiplier1_12_co), .co(multiplier1_8_co),
    .x_c(multiplier1_8_x_c), .s(multiplier1_8_s));
  Multiplier1 multiplier1_9 (
    .x(multiplier1_12_x_c), .y(in_7), .b(multiplier1_8_s), .ci(multiplier1_13_co), .co(multiplier1_9_co),
    .x_c(multiplier1_9_x_c), .s(multiplier1_9_s));
  Multiplier1 multiplier1_10 (
    .x(multiplier1_13_x_c), .y(in_8), .b(multiplier1_9_s), .ci(1'b0), .co(multiplier1_10_co), .s(out_13));  // open: x_c
  Multiplier1 multiplier1_11 (
    .x(x2), .y(in_5), .b(1'b0), .ci(multiplier1_14_co), .co(multiplier1_11_co), .x_c(multiplier1_11_x_c),
    .s(multiplier1_11_s));
  Multiplier1 multiplier1_12 (
    .x(multiplier1_14_x_c), .y(in_6), .b(multiplier1_11_s), .ci(multiplier1_15_co), .co(multiplier1_12_co),
    .x_c(multiplier1_12_x_c), .s(multiplier1_12_s));
  Multiplier1 multiplier1_13 (
    .x(multiplier1_15_x_c), .y(in_7), .b(multiplier1_12_s), .ci(1'b0), .co(multiplier1_13_co),
    .x_c(multiplier1_13_x_c), .s(out_14));
  Multiplier1 multiplier1_14 (
    .x(x1), .y(in_5), .b(1'b0), .ci(multiplier1_16_co), .co(multiplier1_14_co), .x_c(multiplier1_14_x_c),
    .s(multiplier1_14_s));
  Multiplier1 multiplier1_15 (
    .x(multiplier1_16_x_c), .y(in_6), .b(multiplier1_14_s), .ci(1'b0), .co(multiplier1_15_co),
    .x_c(multiplier1_15_x_c), .s(out_15));
  Multiplier1 multiplier1_16 (
    .x(x0), .y(in_5), .b(1'b0), .ci(1'b0), .co(multiplier1_16_co), .x_c(multiplier1_16_x_c), .s(out_16));
endmodule
