// Logisim project devices.circ as structural Verilog: 1 circuit, main circuit main
module main (
  input  D7,
  input  D6,
  input  D5,
  input  D4,
  input  D3,
  input  D2,
  input  D1,
  input  D0,
  input  [7:0] in_9,
  input  [3:0] in_10,
  input  [1:0] in_11,
  input  [1:0] in_12,
  output Y0,
  output Y1,
  output Y2,
  output Y3,
  output Y4,
  output Y5,
  output Y6,
  output Y7,
  output [7:0] out_21,
  output [2:0] out_22,
  output [3:0] out_23
);

  wire multiplexer_1_out, not_1_out, not_2_out, not_3_out, or_1_out, or_2_out, or_3_out;

  Priority_Encoder priority_encoder_1 (
    .in0(in_9[0]), .in1(in_9[1]), .in2(in_9[2]), .in3(in_9[3]), .in4(in_9[4]), .in5(in_9[5]), .in6(in_9[6]),
    .in7(in_9[7]), .out(out_22));  // open: en_in, gs, en_out
  Multiplexer #(.select(2)) multiplexer_1 (
    .in0(in_10[0]), .in1(in_10[1]), .in2(in_10[2]), .in3(in_10[3]), .out(multiplexer_1_out), .sel(in_11));
  or or_1 (or_1_out, D4, D5, D6, D7);
  or or_2 (or_2_out, D2, D3, D6, D7);
  or or_3 (or_3_out, D1, D3, D5, D7);
  Decoder #(.select(3)) decoder_1 (
    .out0(out_21[0]), .out1(out_21[1]), .out2(out_21[2]), .out3(out_21[3]), .out4(out_21[4]),
    .out5(out_21[5]), .out6(out_21[6]), .out7(out_21[7]), .sel(out_22));  // open: en
  Demultiplexer #(.select(2)) demultiplexer_1 (
    .out0(out_23[0]), .out1(out_23[1]), .out2(out_23[2]), .out3(out_23[3]), .in(multiplexer_1_out),
    .sel(in_12));
  not not_1 (not_1_out, or_1_out);
  not not_2 (not_2_out, or_2_out);
  not not_3 (not_3_out, or_3_out);
  and and_1 (Y0, not_1_out, not_2_out, not_3_out);
  and and_2 (Y1, not_1_out, not_2_out, or_3_out);
  and and_3 (Y2, not_1_out, or_2_out, not_3_out);
  and and_4 (Y3, not_1_out, or_2_out, or_3_out);
  and and_5 (Y4, or_1_out, not_2_out, not_3_out);
  and and_6 (Y5, or_1_out, not_2_out, or_3_out);
  and and_7 (Y6, or_1_out, or_2_out, not_3_out);
  and and_8 (Y7, or_1_out, or_2_out, or_3_out);

  // Notes on the sheet:
  //   Multiplexer and Demultiplexer
  //   Encoder and Decoder
endmodule
