// Logisim project 4Bit Binary Adder Circuit.circ as structural Verilog: 1 circuit, main circuit main
module main (
  input  in_1,
  input  in_2,
  input  in_3,
  input  in_4,
  input  in_5,
  input  in_6,
  input  in_7,
  input  in_8,
  input  in_9,
  output out_10,
  output out_11,
  output out_12,
  output out_13,
  output out_14
);

  wire adder_2_cout, adder_3_cout, adder_4_cout;

  Adder #(.width(1)) adder_1 (.a(in_5), .b(in_1), .out(out_11), .cin(adder_2_cout), .cout(out_10));
  Adder #(.width(1)) adder_2 (.a(in_6), .b(in_2), .out(out_12), .cin(adder_3_cout), .cout(adder_2_cout));
  Adder #(.width(1)) adder_3 (.a(in_7), .b(in_3), .out(out_13), .cin(adder_4_cout), .cout(adder_3_cout));
  Adder #(.width(1)) adder_4 (.a(in_8), .b(in_4), .out(out_14), .cin(in_9), .cout(adder_4_cout));
endmodule
