// Logisim project 4X16 Decoder Construction 1.circ as structural Verilog: 1 circuit, main circuit main
module main (
  input  W,
  input  X,
  input  [1:0] Y_Z,
  output out_4,
  output out_5,
  output out_6,
  output out_7,
  output out_8,
  output out_9,
  output out_10,
  output out_11,
  output out_12,
  output D8_to_D11,
  output out_14,
  output out_15,
  output out_16,
  output D12_to_D15,
  output out_18,
  output out_19
);

  wire and_1_out, and_2_out, and_3_out, and_4_out, not_1_out, not_2_out;

  not not_1 (not_1_out, W);
  not not_2 (not_2_out, X);
  and and_1 (and_1_out, not_1_out, not_2_out);
  and and_2 (and_2_out, not_1_out, X);
  and and_3 (and_3_out, not_2_out, W);
  and and_4 (and_4_out, W, X);
  Decoder #(.select(2)) decoder_1 (.out0(out_4), .out1(out_5), .out2(out_6), .out3(out_7), .sel(Y_Z), .en(and_1_out));
  Decoder #(.select(2)) decoder_2 (.out0(out_8), .out1(out_9), .out2(out_10), .out3(out_11), .sel(Y_Z), .en(and_2_out));
  Decoder #(.select(2)) decoder_3 (
    .out0(out_12), .out1(D8_to_D11), .out2(out_14), .out3(out_15), .sel(Y_Z), .en(and_3_out));
  Decoder #(.select(2)) decoder_4 (
    .out0(out_16), .out1(D12_to_D15), .out2(out_18), .out3(out_19), .sel(Y_Z), .en(and_4_out));

  // Notes on the sheet:
  //   D0 to D3
  //   D4 to D7
  //   Implementation of 4X16 Decoder using 2X4 Decoders
endmodule
