// Logisim project 4X16 Decoder Construction 2.circ as structural Verilog: 1 circuit, main circuit main
module main (
  input  W,
  input  [2:0] X_Y_Z,
  output out_3,
  output out_4,
  output out_5,
  output out_6,
  output out_7,
  output out_8,
  output out_9,
  output out_10,
  output out_11,
  output out_12,
  output out_13,
  output D8_to_D15,
  output out_15,
  output out_16,
  output out_17,
  output out_18
);

  wire not_1_out;

  not not_1 (not_1_out, W);
  Demultiplexer #(.select(3)) demultiplexer_1 (
    .out0(out_3), .out1(out_4), .out2(out_5), .out3(out_6), .out4(out_7), .out5(out_8), .out6(out_9),
    .out7(out_10), .sel(X_Y_Z), .en(not_1_out));  // open: in
  Demultiplexer #(.select(3)) demultiplexer_2 (
    .out0(out_11), .out1(out_12), .out2(out_13), .out3(D8_to_D15), .out4(out_15), .out5(out_16),
    .out6(out_17), .out7(out_18), .sel(X_Y_Z), .en(W));  // open: in

  // Notes on the sheet:
  //   D0 to DD7
  //   Implementation of 4X16 Decoder using 6X8 Decoder
endmodule
