// Logisim project 4X16 Decoder Construction 3.circ as structural Verilog: 1 circuit, main circuit main
module main (
  input  [2:0] X_Y_Z,
  input  W,
  input  X,
  input  [1:0] Y_Z,
  output out_5,
  output out_6,
  output out_7,
  output out_8,
  output out_9,
  output out_10,
  output out_11,
  output out_12,
  output out_13,
  output out_14,
  output out_15,
  output out_16,
  output out_17,
  output out_18,
  output out_19,
  output out_20
);

  wire and_1_out, and_2_out, not_1_out, not_2_out;

  not not_1 (not_1_out, W);
  not not_2 (not_2_out, X);
  and and_1 (and_1_out, not_1_out, not_2_out);
  and and_2 (and_2_out, not_1_out, X);
  Demultiplexer #(.select(2)) demultiplexer_1 (
    .out0(out_5), .out1(out_6), .out2(out_7), .out3(out_8), .sel(Y_Z), .en(and_1_out));  // open: in
  Demultiplexer #(.select(2)) demultiplexer_2 (
    .out0(out_9), .out1(out_10), .out2(out_11), .out3(out_12), .sel(Y_Z), .en(and_2_out));  // open: in
  Demultiplexer #(.select(3)) demultiplexer_3 (
    .out0(out_13), .out1(out_14), .out2(out_15), .out3(out_16), .out4(out_17), .out5(out_18), .out6(out_19),
    .out7(out_20), .sel(X_Y_Z), .en(W));  // open: in

  // Notes on the sheet:
  //   D0 to D3
  //   D4 to D7
  //   D8 to D15
  //   Implementation of 4X16 Decoder using 2X4 and 3X8 Decoders
endmodule
