// Logisim project 8_BitsAdder.circ as structural Verilog: 1 circuit, main circuit main
module main (
  input  in_1,
  input  in_2,
  input  in_3,
  input  in_4,
  input  Binary_Input_2,
  input  in_6,
  input  in_7,
  input  in_8,
  input  in_9,
  input  in_10,
  input  in_11,
  input  in_12,
  input  in_13,
  input  in_14,
  input  in_15,
  input  in_16,
  input  in_17,
  output out_18,
  output out_19,
  output out_20,
  output out_21,
  output out_22,
  output out_23,
  output out_24,
  output out_25,
  output out_26
);

  wire adder_2_cout, adder_3_cout, adder_4_cout, adder_5_cout, adder_6_cout, adder_7_cout, adder_8_cout;

  Adder #(.width(1)) adder_1 (.a(in_14), .b(Binary_Input_2), .out(out_19), .cin(adder_2_cout), .cout(out_18));
  Adder #(.width(1)) adder_2 (.a(in_15), .b(in_6), .out(out_20), .cin(adder_3_cout), .cout(adder_2_cout));
  Adder #(.width(1)) adder_3 (.a(in_16), .b(in_7), .out(out_21), .cin(adder_4_cout), .cout(adder_3_cout));
  Adder #(.width(1)) adder_4 (.a(in_17), .b(in_8), .out(out_22), .cin(adder_5_cout), .cout(adder_4_cout));
  Adder #(.width(1)) adder_5 (.a(in_10), .b(in_1), .out(out_23), .cin(adder_6_cout), .cout(adder_5_cout));
  Adder #(.width(1)) adder_6 (.a(in_11), .b(in_2), .out(out_24), .cin(adder_7_cout), .cout(adder_6_cout));
  Adder #(.width(1)) adder_7 (.a(in_12), .b(in_3), .out(out_25), .cin(adder_8_cout), .cout(adder_7_cout));
  Adder #(.width(1)) adder_8 (.a(in_13), .b(in_4), .out(out_26), .cin(in_9), .cout(adder_8_cout));

  // Notes on the sheet:
  //   Binart Input 1
  //   Output
  //   8 Bits BinaryAdder Circuit
  //   Always 0
endmodule
