// Logisim project Assignment.circ as structural Verilog: 1 circuit, main circuit main
module main (
  input  A,
  input  B,
  input  C,
  input  D,
  output T3,
  output F1,
  output T1,
  output T2,
  output T4,
  output F2,
  output Q1,
  output Q2
);

  wire Clk_out, d_ff_1_qn, J_out, K_out, not_1_out, not_2_out, not_3_out, not_4_out;

  Clock Clk (.out(Clk_out));
  not not_1 (not_1_out, Clk_out);
  not not_2 (not_2_out, B);
  not not_3 (not_3_out, A);
  Clock J (.out(J_out));
  Clock K (.out(K_out));
  and and_1 (T1, not_2_out, C);
  and and_2 (T2, not_3_out, B);
  J_K_Flip_Flop j_k_ff_1 (.J(J_out), .clk(not_1_out), .K(K_out), .Q(Q1));  // open: Qn, preset, en, reset
  not not_4 (not_4_out, D);
  or or_1 (T3, A, T1);
  or or_2 (F2, T2, not_4_out);
  D_Flip_Flop d_ff_1 (.clk(Q1), .D(d_ff_1_qn), .Q(Q2), .Qn(d_ff_1_qn));  // open: preset, en, reset
  xor xor_1 (T4, T2, D);
  or or_3 (F1, T3, T4);

  // Notes on the sheet:
  //   Q1
  //   Q2
endmodule
