// Logisim project BCD Adder.circ as structural Verilog: 1 circuit, main circuit main
module main (
  input  in_1,
  input  in_2,
  input  in_3,
  input  in_4,
  input  in_5,
  input  in_6,
  input  in_7,
  input  in_8,
  input  in_9,
  input  in_10,
  input  in_11,
  output out_12,
  output out_13,
  output out_14,
  output out_15,
  output out_16,
  output out_17
);

  wire adder_2_cout, adder_2_out, adder_3_cout, adder_4_cout, adder_4_out, adder_5_cout, adder_6_cout,
       adder_6_out, adder_7_cout, adder_7_out, adder_8_cout, and_1_out, and_2_out;

  or or_1 (out_13, adder_2_cout, and_1_out, and_2_out);
  Adder #(.width(1)) adder_1 (.a(adder_2_out), .b(in_10), .out(out_14), .cin(adder_3_cout), .cout(out_12));
  Adder #(.width(1)) adder_2 (.a(in_5), .b(in_1), .out(adder_2_out), .cin(adder_4_cout), .cout(adder_2_cout));
  and and_1 (and_1_out, adder_2_out, adder_4_out);
  and and_2 (and_2_out, adder_2_out, adder_6_out);
  Adder #(.width(1)) adder_3 (.a(adder_4_out), .b(out_13), .out(out_15), .cin(adder_5_cout), .cout(adder_3_cout));
  Adder #(.width(1)) adder_4 (.a(in_6), .b(in_2), .out(adder_4_out), .cin(adder_6_cout), .cout(adder_4_cout));
  Adder #(.width(1)) adder_5 (.a(adder_6_out), .b(out_13), .out(out_16), .cin(adder_8_cout), .cout(adder_5_cout));
  Adder #(.width(1)) adder_6 (.a(in_7), .b(in_3), .out(adder_6_out), .cin(adder_7_cout), .cout(adder_6_cout));
  Adder #(.width(1)) adder_7 (.a(in_8), .b(in_4), .out(adder_7_out), .cin(in_9), .cout(adder_7_cout));
  Adder #(.width(1)) adder_8 (.a(adder_7_out), .b(in_10), .out(out_17), .cin(in_11), .cout(adder_8_cout));
endmodule
