// Logisim project Binary Subtractor.circ as structural Verilog: 1 circuit, main circuit main
module main (
  input  in_1,
  input  in_2,
  input  in_3,
  input  in_4,
  input  in_5,
  input  in_6,
  input  in_7,
  input  in_8,
  input  in_9,
  output out_10,
  output out_11,
  output out_12,
  output out_13,
  output out_14
);

  wire adder_2_cout, adder_3_cout, adder_4_cout, undriven, xor_1_out, xor_2_out, xor_3_out, xor_4_out;

  xor xor_1 (xor_1_out, in_5, in_9);
  xor xor_2 (xor_2_out, in_6, in_9);
  Adder #(.width(1)) adder_1 (.a(in_1), .b(xor_1_out), .out(out_11), .cin(adder_2_cout), .cout(out_10));
  xor xor_3 (xor_3_out, in_7, in_9);
  Adder #(.width(1)) adder_2 (.a(in_2), .b(xor_2_out), .out(out_12), .cin(adder_3_cout), .cout(adder_2_cout));
  Adder #(.width(1)) adder_3 (.a(in_3), .b(xor_3_out), .out(out_13), .cin(adder_4_cout), .cout(adder_3_cout));
  xor xor_4 (xor_4_out, in_8, in_9);
  Adder #(.width(1)) adder_4 (.a(in_4), .b(xor_4_out), .out(out_14), .cin(undriven), .cout(adder_4_cout));

  // Notes on the sheet:
  //   M = 0, Adder
  //   M = 1, Subtractor
endmodule
