// Logisim project BinaryToGrayCode.circ as structural Verilog: 1 circuit, main circuit main
module main (
  input  b7,
  input  b6,
  input  b5,
  input  b4,
  input  b3,
  input  b2,
  input  b1,
  input  b0,
  output g0,
  output g1,
  output g2,
  output g3,
  output g4,
  output g5,
  output g6,
  output g7
);

  xor xor_1 (g0, b0, b1);
  xor xor_2 (g1, b1, b2);
  xor xor_3 (g2, b2, b3);
  xor xor_4 (g3, b3, b4);
  xor xor_5 (g4, b4, b5);
  xor xor_6 (g5, b5, b6);
  xor xor_7 (g6, b6, b7);

  assign g7 = b7;

  // Notes on the sheet:
  //   Binary Code to Gray Code
endmodule
