// Logisim project Asynchronous Counter.circ as structural Verilog: 1 circuit, main circuit main
module main (
  input  in_1,
  input  in_2,
  output out_3,
  output out_4,
  output out_5,
  output out_6,
  output out_7,
  output out_8,
  output out_9,
  output out_10
);

  wire clock_1_out, clock_2_out, j_k_ff_2_qn, j_k_ff_4_qn, j_k_ff_6_qn, Reset_2_out, Reset_out;

  Clock clock_1 (.out(clock_1_out));
  Button Reset (.out(Reset_out));
  Clock clock_2 (.out(clock_2_out));
  Button Reset_2 (.out(Reset_2_out));
  J_K_Flip_Flop j_k_ff_1 (.J(in_1), .clk(clock_1_out), .K(in_1), .Q(out_6), .reset(Reset_out));  // open: Qn, preset, en
  J_K_Flip_Flop j_k_ff_2 (
    .J(in_2), .clk(clock_2_out), .K(in_2), .Q(out_10), .Qn(j_k_ff_2_qn), .reset(Reset_2_out));  // open: preset, en
  J_K_Flip_Flop j_k_ff_3 (.J(in_1), .clk(out_6), .K(in_1), .Q(out_5), .reset(Reset_out));  // open: Qn, preset, en
  J_K_Flip_Flop j_k_ff_4 (
    .J(in_2), .clk(j_k_ff_2_qn), .K(in_2), .Q(out_9), .Qn(j_k_ff_4_qn), .reset(Reset_2_out));  // open: preset, en
  J_K_Flip_Flop j_k_ff_5 (.J(in_1), .clk(out_5), .K(in_1), .Q(out_4), .reset(Reset_out));  // open: Qn, preset, en
  J_K_Flip_Flop j_k_ff_6 (
    .J(in_2), .clk(j_k_ff_4_qn), .K(in_2), .Q(out_8), .Qn(j_k_ff_6_qn), .reset(Reset_2_out));  // open: preset, en
  J_K_Flip_Flop j_k_ff_7 (.J(in_1), .clk(out_4), .K(in_1), .Q(out_3), .reset(Reset_out));  // open: Qn, preset, en
  J_K_Flip_Flop j_k_ff_8 (
    .J(in_2), .clk(j_k_ff_6_qn), .K(in_2), .Q(out_7), .reset(Reset_2_out));  // open: Qn, preset, en

  // Notes on the sheet:
  //   Asynchronous Counter
  //   Count Up ( 0 to 15 )
  //   Count Down (15 to 0)
endmodule
