// Logisim project Asynchronous T D.circ as structural Verilog: 1 circuit, main circuit main
module main (
  input  in_1,
  input  in_2,
  output out_3,
  output out_4,
  output out_5,
  output out_6,
  output out_7,
  output out_8,
  output out_9,
  output out_10,
  output out_11,
  output out_12,
  output out_13,
  output out_14,
  output out_15,
  output out_16,
  output out_17,
  output out_18
);

  wire clock_1_out, clock_2_out, clock_3_out, clock_4_out, d_ff_1_qn, d_ff_2_qn, d_ff_3_qn, d_ff_4_qn,
       d_ff_5_qn, d_ff_6_qn, d_ff_7_qn, d_ff_8_qn, Reset_2_out, Reset_3_out, Reset_4_out, Reset_out,
       t_ff_5_qn, t_ff_6_qn, t_ff_7_qn;

  Clock clock_1 (.out(clock_1_out));
  Button Reset (.out(Reset_out));
  Clock clock_2 (.out(clock_2_out));
  Button Reset_2 (.out(Reset_2_out));
  T_Flip_Flop t_ff_1 (.clk(clock_1_out), .T(in_1), .Q(out_6), .reset(Reset_out));  // open: Qn, preset, en
  D_Flip_Flop d_ff_1 (
    .clk(clock_2_out), .D(d_ff_1_qn), .Q(out_14), .Qn(d_ff_1_qn), .reset(Reset_2_out));  // open: preset, en
  T_Flip_Flop t_ff_2 (.clk(out_6), .T(in_1), .Q(out_5), .reset(Reset_out));  // open: Qn, preset, en
  D_Flip_Flop d_ff_2 (
    .clk(out_14), .D(d_ff_2_qn), .Q(out_13), .Qn(d_ff_2_qn), .reset(Reset_2_out));  // open: preset, en
  T_Flip_Flop t_ff_3 (.clk(out_5), .T(in_1), .Q(out_4), .reset(Reset_out));  // open: Qn, preset, en
  D_Flip_Flop d_ff_3 (
    .clk(out_13), .D(d_ff_3_qn), .Q(out_12), .Qn(d_ff_3_qn), .reset(Reset_2_out));  // open: preset, en
  T_Flip_Flop t_ff_4 (.clk(out_4), .T(in_1), .Q(out_3), .reset(Reset_out));  // open: Qn, preset, en
  D_Flip_Flop d_ff_4 (
    .clk(out_12), .D(d_ff_4_qn), .Q(out_11), .Qn(d_ff_4_qn), .reset(Reset_2_out));  // open: preset, en
  Clock clock_3 (.out(clock_3_out));
  Button Reset_3 (.out(Reset_3_out));
  Clock clock_4 (.out(clock_4_out));
  Button Reset_4 (.out(Reset_4_out));
  T_Flip_Flop t_ff_5 (
    .clk(clock_3_out), .T(in_2), .Q(out_10), .Qn(t_ff_5_qn), .reset(Reset_3_out));  // open: preset, en
  D_Flip_Flop d_ff_5 (
    .clk(clock_4_out), .D(d_ff_5_qn), .Q(out_18), .Qn(d_ff_5_qn), .reset(Reset_4_out));  // open: preset, en
  T_Flip_Flop t_ff_6 (.clk(t_ff_5_qn), .T(in_2), .Q(out_9), .Qn(t_ff_6_qn), .reset(Reset_3_out));  // open: preset, en
  D_Flip_Flop d_ff_6 (
    .clk(d_ff_5_qn), .D(d_ff_6_qn), .Q(out_17), .Qn(d_ff_6_qn), .reset(Reset_4_out));  // open: preset, en
  T_Flip_Flop t_ff_7 (.clk(t_ff_6_qn), .T(in_2), .Q(out_8), .Qn(t_ff_7_qn), .reset(Reset_3_out));  // open: preset, en
  D_Flip_Flop d_ff_7 (
    .clk(d_ff_6_qn), .D(d_ff_7_qn), .Q(out_16), .Qn(d_ff_7_qn), .reset(Reset_4_out));  // open: preset, en
  T_Flip_Flop t_ff_8 (.clk(t_ff_7_qn), .T(in_2), .Q(out_7), .reset(Reset_3_out));  // open: Qn, preset, en
  D_Flip_Flop d_ff_8 (
    .clk(d_ff_7_qn), .D(d_ff_8_qn), .Q(out_15), .Qn(d_ff_8_qn), .reset(Reset_4_out));  // open: preset, en

  // Notes on the sheet:
  //   Down Counter using T FF
  //   Down Counter using D FF
  //   Up Counter using T FF
  //   Up Counter using D FF
endmodule
