// Logisim project Synchronous JK 2.circ as structural Verilog: 1 circuit, main circuit main
module main (
  input  M,
  input  in_2,
  output out_3,
  output out_4,
  output out_5,
  output out_6
);

  wire and_1_out, and_2_out, and_3_out, and_4_out, and_5_out, and_6_out, clock_1_out, j_k_ff_1_qn,
       j_k_ff_2_qn, j_k_ff_3_qn, not_1_out, or_1_out, or_2_out, or_3_out;

  Clock clock_1 (.out(clock_1_out));
  not not_1 (not_1_out, M);
  J_K_Flip_Flop j_k_ff_1 (
    .J(in_2), .clk(clock_1_out), .K(in_2), .Q(out_6), .Qn(j_k_ff_1_qn));  // open: preset, en, reset
  and and_1 (and_1_out, M, out_6);
  and and_2 (and_2_out, j_k_ff_1_qn, not_1_out);
  or or_1 (or_1_out, and_1_out, and_2_out);
  J_K_Flip_Flop j_k_ff_2 (
    .J(or_1_out), .clk(clock_1_out), .K(or_1_out), .Q(out_5), .Qn(j_k_ff_2_qn));  // open: preset, en, reset
  and and_3 (and_3_out, and_1_out, out_5);
  and and_4 (and_4_out, j_k_ff_2_qn, and_2_out);
  or or_2 (or_2_out, and_3_out, and_4_out);
  J_K_Flip_Flop j_k_ff_3 (
    .J(or_2_out), .clk(clock_1_out), .K(or_2_out), .Q(out_4), .Qn(j_k_ff_3_qn));  // open: preset, en, reset
  and and_5 (and_5_out, and_3_out, out_4);
  and and_6 (and_6_out, j_k_ff_3_qn, and_4_out);
  or or_3 (or_3_out, and_5_out, and_6_out);
  J_K_Flip_Flop j_k_ff_4 (.J(or_3_out), .clk(clock_1_out), .K(or_3_out), .Q(out_3));  // open: Qn, preset, en, reset
endmodule
