// Logisim project Synchronous T.circ as structural Verilog: 1 circuit, main circuit main
module main (
  input  in_1,
  input  in_2,
  output out_3,
  output out_4,
  output out_5,
  output out_6,
  output out_7,
  output out_8,
  output out_9,
  output out_10
);

  wire and_1_out, and_2_out, and_3_out, and_4_out, clock_1_out, clock_2_out, t_ff_2_qn, t_ff_4_qn, t_ff_6_qn;

  Clock clock_1 (.out(clock_1_out));
  Clock clock_2 (.out(clock_2_out));
  T_Flip_Flop t_ff_1 (.clk(clock_1_out), .T(in_1), .Q(out_6));  // open: Qn, preset, reset, en
  T_Flip_Flop t_ff_2 (.clk(clock_2_out), .T(in_2), .Q(out_10), .Qn(t_ff_2_qn));  // open: preset, reset, en
  T_Flip_Flop t_ff_3 (.clk(clock_1_out), .T(out_6), .Q(out_5));  // open: Qn, preset, reset, en
  T_Flip_Flop t_ff_4 (.clk(clock_2_out), .T(t_ff_2_qn), .Q(out_9), .Qn(t_ff_4_qn));  // open: preset, reset, en
  and and_1 (and_1_out, out_6, out_5);
  and and_2 (and_2_out, t_ff_2_qn, t_ff_4_qn);
  T_Flip_Flop t_ff_5 (.clk(clock_1_out), .T(and_1_out), .Q(out_4));  // open: Qn, preset, reset, en
  T_Flip_Flop t_ff_6 (.clk(clock_2_out), .T(and_2_out), .Q(out_8), .Qn(t_ff_6_qn));  // open: preset, reset, en
  and and_3 (and_3_out, and_1_out, out_4);
  and and_4 (and_4_out, and_2_out, t_ff_6_qn);
  T_Flip_Flop t_ff_7 (.clk(clock_1_out), .T(and_3_out), .Q(out_3));  // open: Qn, preset, reset, en
  T_Flip_Flop t_ff_8 (.clk(clock_2_out), .T(and_4_out), .Q(out_7));  // open: Qn, preset, reset, en

  // Notes on the sheet:
  //   Up Counter
  //   Down Counter
endmodule
