// Logisim project Decade Counter 7 seg.circ as structural Verilog: 1 circuit, main circuit main
module main (
  input  in_1
);

  wire and_1_out, and_2_out, and_3_out, and_4_out, and_5_out, and_6_out, and_7_out, and_8_out, and_9_out,
       and_10_out, and_11_out, and_12_out, clock_1_out, j_k_ff_1_q, j_k_ff_2_q, j_k_ff_3_q, j_k_ff_4_q,
       not_1_out, not_2_out, not_3_out, or_1_out, or_2_out, or_3_out, or_4_out, or_5_out, or_6_out, or_7_out;

  Clock clock_1 (.out(clock_1_out));
  J_K_Flip_Flop j_k_ff_1 (
    .J(in_1), .clk(clock_1_out), .K(in_1), .Q(j_k_ff_1_q), .reset(and_12_out));  // open: Qn, preset, en
  J_K_Flip_Flop j_k_ff_2 (
    .J(j_k_ff_1_q), .clk(clock_1_out), .K(j_k_ff_1_q), .Q(j_k_ff_2_q), .reset(and_12_out));  // open: Qn, preset, en
  and and_1 (and_1_out, j_k_ff_1_q, j_k_ff_2_q);
  not not_1 (not_1_out, j_k_ff_2_q);
  not not_2 (not_2_out, j_k_ff_3_q);
  not not_3 (not_3_out, j_k_ff_1_q);
  J_K_Flip_Flop j_k_ff_3 (
    .J(and_1_out), .clk(clock_1_out), .K(and_1_out), .Q(j_k_ff_3_q), .reset(and_12_out));  // open: Qn, preset, en
  and and_2 (and_2_out, j_k_ff_3_q, j_k_ff_1_q);
  and and_3 (and_3_out, not_2_out, not_3_out);
  and and_4 (and_4_out, j_k_ff_2_q, j_k_ff_1_q);
  and and_5 (and_5_out, not_1_out, not_3_out);
  and and_6 (and_6_out, j_k_ff_3_q, not_1_out, j_k_ff_1_q);
  and and_7 (and_7_out, not_3_out, j_k_ff_2_q);
  and and_8 (and_8_out, not_1_out, j_k_ff_3_q);
  and and_9 (and_9_out, not_3_out, j_k_ff_3_q);
  and and_10 (and_10_out, and_1_out, j_k_ff_3_q);
  and and_11 (and_11_out, j_k_ff_2_q, not_2_out);
  J_K_Flip_Flop j_k_ff_4 (
    .J(and_10_out), .clk(clock_1_out), .K(and_10_out), .Q(j_k_ff_4_q), .reset(and_12_out));  // open: Qn, preset, en
  and and_12 (and_12_out, j_k_ff_4_q, j_k_ff_2_q);
  or or_1 (or_1_out, and_2_out, and_3_out, j_k_ff_4_q, j_k_ff_2_q);
  or or_2 (or_2_out, and_4_out, and_5_out, not_2_out);
  or or_3 (or_3_out, j_k_ff_3_q, not_1_out, j_k_ff_1_q);
  or or_4 (or_4_out, and_6_out, and_7_out, and_3_out, and_11_out, j_k_ff_4_q);
  or or_5 (or_5_out, and_3_out, and_7_out);
  or or_6 (or_6_out, and_5_out, and_9_out, and_8_out, j_k_ff_4_q);
  or or_7 (or_7_out, j_k_ff_4_q, and_7_out, and_8_out, and_11_out);
  _7_Segment_Display u_7_segment_display_1 (
    .g(or_7_out), .f(or_6_out), .a(or_1_out), .b(or_2_out), .e(or_5_out), .d(or_4_out), .c(or_3_out));  // open: dp
endmodule
