// Logisim project Decoder.circ as structural Verilog: 1 circuit, main circuit main
module main (
  input  X,
  input  Y,
  input  Z,
  output out_4,
  output out_5,
  output out_6,
  output out_7,
  output out_8,
  output out_9,
  output out_10,
  output out_11
);

  wire not_1_out, not_2_out, not_3_out;

  not not_1 (not_1_out, X);
  not not_2 (not_2_out, Y);
  not not_3 (not_3_out, Z);
  and D0 (out_4, not_1_out, not_2_out, not_3_out);
  and D1 (out_5, not_1_out, not_2_out, Z);
  and D2 (out_6, not_1_out, Y, not_3_out);
  and D3 (out_7, not_1_out, Y, Z);
  and D4 (out_8, X, not_2_out, not_3_out);
  and D5 (out_9, X, not_2_out, Z);
  and D6 (out_10, X, Y, not_3_out);
  and D7 (out_11, X, Y, Z);

  // Notes on the sheet:
  //   DECODER
endmodule
