// Logisim project EncoderDecoder.circ as structural Verilog: 1 circuit, main circuit main
module main (
  input  D0,
  input  D1,
  input  D2,
  input  D3,
  input  D4,
  input  D5,
  input  D6,
  input  D7,
  output D0_2,
  output D1_2,
  output D2_2,
  output X,
  output Y,
  output Z,
  output D3_2,
  output D4_2,
  output D5_2,
  output D6_2,
  output D7_2
);

  wire not_1_out, not_2_out, not_3_out;

  or or_1 (X, D4, D5, D6, D7);
  or or_2 (Y, D2, D3, D6, D7);
  or or_3 (Z, D3, D1, D5, D7);
  not not_1 (not_1_out, X);
  not not_2 (not_2_out, Y);
  not not_3 (not_3_out, Z);
  and and_1 (D0_2, not_1_out, not_2_out, not_3_out);
  and and_2 (D1_2, not_1_out, not_2_out, Z);
  and and_3 (D2_2, not_1_out, Y, not_3_out);
  and and_4 (D3_2, not_1_out, Y, Z);
  and and_5 (D4_2, X, not_2_out, not_3_out);
  and and_6 (D5_2, X, not_2_out, Z);
  and and_7 (D6_2, X, Y, not_3_out);
  and and_8 (D7_2, X, Y, Z);
endmodule
