// Logisim project D.circ as structural Verilog: 1 circuit, main circuit main
module main (
  input  D,
  input  D_2,
  output Q,
  output Q_prime,
  output out_5,
  output out_6
);

  wire clock_1_out, nand_1_out, nand_2_out, not_1_out, not_2_out;

  Clock clock_1 (.out(clock_1_out));
  not not_1 (not_1_out, D);
  not not_2 (not_2_out, D_2);
  nand nand_1 (nand_1_out, D_2, clock_1_out);
  nand nand_2 (nand_2_out, clock_1_out, not_2_out);
  nand nand_3 (Q, not_1_out, Q_prime);
  nand nand_4 (Q_prime, Q, D);
  nand nand_5 (out_5, nand_1_out, out_6);
  nand nand_6 (out_6, out_5, nand_2_out);
endmodule
