// Logisim project JK.circ as structural Verilog: 1 circuit, main circuit main
module main (
  input  J,
  input  K,
  input  K_2,
  input  J_2,
  input  J_3,
  input  K_3,
  output Q,
  output Q_2,
  output Q_prime,
  output Q_prime_2,
  output Q_3,
  output Qnot
);

  wire and_1_out, and_2_out, clock_1_out, nand_1_out, nand_2_out, nand_3_out, nand_4_out, nand_7_out,
       nand_8_out, nand_9_out, nand_10_out, not_1_out;

  Clock clock_1 (.out(clock_1_out));
  nand nand_1 (nand_1_out, Q_prime, J);
  nand nand_2 (nand_2_out, K_2, Q);
  nand nand_3 (nand_3_out, Qnot, J_3, clock_1_out);
  nand nand_4 (nand_4_out, clock_1_out, K_3, Q_3);
  nand nand_5 (Q, nand_1_out, Q_prime);
  nand nand_6 (Q_prime, Q, nand_2_out);
  nand nand_7 (nand_7_out, nand_3_out, nand_8_out);
  nand nand_8 (nand_8_out, nand_7_out, nand_4_out);
  not not_1 (not_1_out, clock_1_out);
  and and_1 (and_1_out, Q_2, K);
  and and_2 (and_2_out, J_2, Q_prime_2);
  nand nand_9 (nand_9_out, nand_7_out, not_1_out);
  nand nand_10 (nand_10_out, not_1_out, nand_8_out);
  nor nor_1 (Q_2, and_1_out, Q_prime_2);
  nor nor_2 (Q_prime_2, Q_2, and_2_out);
  nand nand_11 (Q_3, nand_9_out, Qnot);
  nand nand_12 (Qnot, Q_3, nand_10_out);
endmodule
