// Logisim project SR.circ as structural Verilog: 1 circuit, main circuit main
module main (
  input  S,
  input  R,
  input  R_2,
  input  S_2,
  input  R_3,
  input  S_3,
  output Q,
  output Q_2,
  output Q_prime,
  output Q_prime_2,
  output Q_3,
  output Q_prime_3
);

  wire and_1_out, and_2_out, clock_1_out;

  nand nand_1 (Q, S, Q_prime);
  nand nand_2 (Q_prime, Q, R_2);
  Clock clock_1 (.out(clock_1_out));
  and and_1 (and_1_out, R_3, clock_1_out);
  and and_2 (and_2_out, clock_1_out, S_3);
  nor nor_1 (Q_2, R, Q_prime_2);
  nor nor_2 (Q_prime_2, Q_2, S_2);
  nor nor_3 (Q_3, and_1_out, Q_prime_3);
  nor nor_4 (Q_prime_3, Q_3, and_2_out);
endmodule
