// Logisim project T.circ as structural Verilog: 1 circuit, main circuit main
module main (
  input  T,
  input  T_2,
  output Q,
  output Q_prime,
  output Q_2,
  output Qnot
);

  wire clock_1_out, nand_1_out, nand_2_out, nand_3_out, nand_4_out, nand_5_out, nand_6_out, nand_9_out,
       nand_10_out, not_1_out;

  Clock clock_1 (.out(clock_1_out));
  nand nand_1 (nand_1_out, Qnot, T_2, clock_1_out);
  nand nand_2 (nand_2_out, clock_1_out, T_2, Q_2);
  nand nand_3 (nand_3_out, Q_prime, T);
  nand nand_4 (nand_4_out, T, Q);
  not not_1 (not_1_out, clock_1_out);
  nand nand_5 (nand_5_out, nand_1_out, nand_6_out);
  nand nand_6 (nand_6_out, nand_5_out, nand_2_out);
  nand nand_7 (Q, nand_3_out, Q_prime);
  nand nand_8 (Q_prime, Q, nand_4_out);
  nand nand_9 (nand_9_out, nand_5_out, not_1_out);
  nand nand_10 (nand_10_out, not_1_out, nand_6_out);
  nand nand_11 (Q_2, nand_9_out, Qnot);
  nand nand_12 (Qnot, Q_2, nand_10_out);
endmodule
