// Logisim project GrayToBinary.circ as structural Verilog: 1 circuit, main circuit main
module main (
  input  g7,
  input  g6,
  input  g5,
  input  g4,
  input  g3,
  input  g2,
  input  g1,
  input  g0,
  output b0,
  output b1,
  output b2,
  output b3,
  output b4,
  output b5,
  output b6,
  output b7
);

  xor xor_1 (b0, g0, g1);
  xor xor_2 (b1, g1, g2);
  xor xor_3 (b2, g2, g3);
  xor xor_4 (b3, g3, g4);
  xor xor_5 (b4, g4, g5);
  xor xor_6 (b5, g5, g6);
  xor xor_7 (b6, g6, g7);

  assign b7 = g7;

  // Notes on the sheet:
  //   Gray Code to Binary Code
endmodule
