// Logisim project JK Flip Flop.circ as structural Verilog: 1 circuit, main circuit main
module main (
  input  J,
  input  K,
  input  J_2,
  input  K_2,
  output Q,
  output Qnot,
  output Q_2,
  output Qnot_2
);

  wire clock_1_out, clock_2_out, nand_1_out, nand_2_out, nand_3_out, nand_4_out, nand_7_out, nand_8_out,
       nand_9_out, nand_10_out, not_1_out;

  Clock clock_1 (.out(clock_1_out));
  Clock clock_2 (.out(clock_2_out));
  nand nand_1 (nand_1_out, Qnot, J, clock_1_out);
  nand nand_2 (nand_2_out, clock_1_out, K, Q);
  nand nand_3 (nand_3_out, Qnot_2, J_2, clock_2_out);
  nand nand_4 (nand_4_out, clock_2_out, K_2, Q_2);
  not not_1 (not_1_out, clock_2_out);
  nand nand_5 (Q, nand_1_out, Qnot);
  nand nand_6 (Qnot, Q, nand_2_out);
  nand nand_7 (nand_7_out, nand_3_out, nand_8_out);
  nand nand_8 (nand_8_out, nand_7_out, nand_4_out);
  nand nand_9 (nand_9_out, nand_7_out, not_1_out);
  nand nand_10 (nand_10_out, not_1_out, nand_8_out);
  nand nand_11 (Qnot_2, Q_2, nand_10_out);
  nand nand_12 (Q_2, nand_9_out, Qnot_2);
endmodule
