// Logisim project D and T Clocked.circ as structural Verilog: 1 circuit, main circuit main
module main (
  input  D,
  input  T,
  output out_3,
  output out_4,
  output Q,
  output Qnot
);

  wire clock_1_out, clock_2_out, nand_1_out, nand_2_out, nand_3_out, nand_4_out, nand_7_out, nand_8_out,
       nand_9_out, nand_10_out, not_1_out, not_2_out;

  Clock clock_1 (.out(clock_1_out));
  Clock clock_2 (.out(clock_2_out));
  nand nand_1 (nand_1_out, Qnot, T, clock_1_out);
  nand nand_2 (nand_2_out, clock_1_out, T, Q);
  not not_1 (not_1_out, D);
  nand nand_3 (nand_3_out, D, clock_2_out);
  nand nand_4 (nand_4_out, not_1_out, clock_2_out);
  not not_2 (not_2_out, clock_1_out);
  nand nand_5 (out_3, nand_3_out, out_4);
  nand nand_6 (out_4, out_3, nand_4_out);
  nand nand_7 (nand_7_out, nand_1_out, nand_8_out);
  nand nand_8 (nand_8_out, nand_7_out, nand_2_out);
  nand nand_9 (nand_9_out, nand_7_out, not_2_out);
  nand nand_10 (nand_10_out, not_2_out, nand_8_out);
  nand nand_11 (Q, nand_9_out, Qnot);
  nand nand_12 (Qnot, Q, nand_10_out);
endmodule
