// Logisim project D and T.circ as structural Verilog: 1 circuit, main circuit main
module main (
  input  D,
  input  T,
  output Q,
  output Q_prime,
  output Q_2,
  output Q_prime_2
);

  wire nand_1_out, nand_2_out, not_1_out;

  not not_1 (not_1_out, D);
  nand nand_1 (nand_1_out, Q_prime_2, T);
  nand nand_2 (nand_2_out, T, Q_2);
  nand nand_3 (Q, not_1_out, Q_prime);
  nand nand_4 (Q_prime, Q, D);
  nand nand_5 (Q_2, nand_1_out, Q_prime_2);
  nand nand_6 (Q_prime_2, Q_2, nand_2_out);
endmodule
