// Logisim project Flip Flop Module.circ as structural Verilog: 1 circuit, main circuit main
module main (
  input  in_1,
  input  in_2,
  input  in_3,
  input  in_4,
  input  in_5,
  input  in_6,
  output out_7,
  output out_8,
  output out_9,
  output out_10,
  output out_11,
  output out_12,
  output out_13,
  output out_14
);

  wire clock_1_out, clock_2_out, clock_3_out, clock_4_out;

  Clock clock_1 (.out(clock_1_out));
  Clock clock_2 (.out(clock_2_out));
  Clock clock_3 (.out(clock_3_out));
  Clock clock_4 (.out(clock_4_out));
  S_R_Flip_Flop s_r_ff_1 (.S(in_1), .clk(clock_1_out), .R(in_2), .Q(out_7), .Qn(out_8));  // open: preset, reset, en
  J_K_Flip_Flop j_k_ff_1 (.J(in_3), .clk(clock_2_out), .K(in_4), .Q(out_9), .Qn(out_10));  // open: preset, en, reset
  D_Flip_Flop d_ff_1 (.clk(clock_3_out), .D(in_5), .Q(out_11), .Qn(out_12));  // open: preset, en, reset
  T_Flip_Flop t_ff_1 (.clk(clock_4_out), .T(in_6), .Q(out_13), .Qn(out_14));  // open: preset, reset, en
endmodule
