// Logisim project JK.circ as structural Verilog: 1 circuit, main circuit main
module main (
  input  J,
  input  K,
  input  K_2,
  input  J_2,
  output Q,
  output Q_prime,
  output Q_2,
  output Q_prime_2
);

  wire and_1_out, and_2_out, nand_1_out, nand_2_out;

  nand nand_1 (nand_1_out, Q_prime, J);
  nand nand_2 (nand_2_out, K, Q);
  and and_1 (and_1_out, Q_2, K_2);
  and and_2 (and_2_out, J_2, Q_prime_2);
  nand nand_3 (Q, nand_1_out, Q_prime);
  nand nand_4 (Q_prime, Q, nand_2_out);
  nor nor_1 (Q_2, and_1_out, Q_prime_2);
  nor nor_2 (Q_prime_2, Q_2, and_2_out);
endmodule
