// Logisim project Multiplexer and Decoder.circ as structural Verilog: 1 circuit, main circuit main
module main (
  input  in_1,
  input  in_2,
  input  in_3,
  input  in_4,
  input  in_5,
  input  in_6,
  input  in_7,
  input  in_8,
  input  [2:0] in_9,
  input  [2:0] in_10,
  output out_11,
  output out_12,
  output out_13,
  output out_14,
  output out_15,
  output out_16,
  output out_17,
  output out_18,
  output out_19
);

  Multiplexer #(.select(3)) multiplexer_1 (
    .in0(in_1), .in1(in_2), .in2(in_3), .in3(in_4), .in4(in_5), .in5(in_6), .in6(in_7), .in7(in_8),
    .out(out_15), .sel(in_10));  // open: en
  Decoder #(.select(3)) decoder_1 (
    .out0(out_11), .out1(out_12), .out2(out_13), .out3(out_14), .out4(out_16), .out5(out_17), .out6(out_18),
    .out7(out_19), .sel(in_9));  // open: en
endmodule
