// Logisim project SR.circ as structural Verilog: 1 circuit, main circuit main
module main (
  input  R,
  input  R_2,
  input  S,
  input  S_2,
  output Q,
  output Q_2,
  output Q_prime,
  output Q_prime_2
);

  nand nand_1 (Q, R, Q_prime);
  nand nand_2 (Q_prime, Q, S);
  nor nor_1 (Q_2, R_2, Q_prime_2);
  nor nor_2 (Q_prime_2, Q_2, S_2);
endmodule
