// Logisim project Synchronous Counter.circ as structural Verilog: 1 circuit, main circuit main
module main (
  input  in_1,
  input  in_2,
  output out_3,
  output out_4,
  output out_5,
  output out_6,
  output out_7,
  output out_8,
  output out_9,
  output out_10
);

  wire and_1_out, and_2_out, and_3_out, and_4_out, clock_1_out, clock_2_out, j_k_ff_2_qn, j_k_ff_3_qn,
       j_k_ff_6_qn, Reset_2_out, Reset_out;

  Button Reset (.out(Reset_out));
  Clock clock_1 (.out(clock_1_out));
  Button Reset_2 (.out(Reset_2_out));
  Clock clock_2 (.out(clock_2_out));
  J_K_Flip_Flop j_k_ff_1 (.J(in_1), .clk(clock_1_out), .K(in_1), .Q(out_6), .reset(Reset_out));  // open: Qn, preset, en
  J_K_Flip_Flop j_k_ff_2 (
    .J(in_2), .clk(clock_2_out), .K(in_2), .Q(out_10), .Qn(j_k_ff_2_qn), .reset(Reset_2_out));  // open: preset, en
  J_K_Flip_Flop j_k_ff_3 (
    .J(j_k_ff_2_qn), .clk(clock_2_out), .K(j_k_ff_2_qn), .Q(out_9), .Qn(j_k_ff_3_qn), .reset(Reset_2_out));  // open: preset, en
  J_K_Flip_Flop j_k_ff_4 (
    .J(out_6), .clk(clock_1_out), .K(out_6), .Q(out_5), .reset(Reset_out));  // open: Qn, preset, en
  and and_1 (and_1_out, out_6, out_5);
  and and_2 (and_2_out, j_k_ff_2_qn, j_k_ff_3_qn);
  J_K_Flip_Flop j_k_ff_5 (
    .J(and_1_out), .clk(clock_1_out), .K(and_1_out), .Q(out_4), .reset(Reset_out));  // open: Qn, preset, en
  J_K_Flip_Flop j_k_ff_6 (
    .J(and_2_out), .clk(clock_2_out), .K(and_2_out), .Q(out_8), .Qn(j_k_ff_6_qn), .reset(Reset_2_out));  // open: preset, en
  and and_3 (and_3_out, and_1_out, out_4);
  and and_4 (and_4_out, and_2_out, j_k_ff_6_qn);
  J_K_Flip_Flop j_k_ff_7 (
    .J(and_3_out), .clk(clock_1_out), .K(and_3_out), .Q(out_3), .reset(Reset_out));  // open: Qn, preset, en
  J_K_Flip_Flop j_k_ff_8 (
    .J(and_4_out), .clk(clock_2_out), .K(and_4_out), .Q(out_7), .reset(Reset_2_out));  // open: Qn, preset, en

  // Notes on the sheet:
  //   Synchronous Counter
  //   Up Count (0 to 15)
  //   Doen count (15 to 0)
endmodule
