// Logisim project x.circ as structural Verilog: 1 circuit, main circuit main
module main (
  input  A,
  input  B,
  input  C,
  input  C_2,
  input  A_2,
  input  B_2,
  input  in_7,
  output Sum,
  output Sum_2,
  output Carry,
  output Carry_2,
  output out_12,
  output out_13,
  output out_14,
  output out_15
);

  wire and_1_out, and_2_out, and_3_out, clock_1_out, j_k_ff_1_qn, j_k_ff_2_qn, j_k_ff_3_qn, xor_1_out;

  Clock clock_1 (.out(clock_1_out));
  J_K_Flip_Flop j_k_ff_1 (
    .J(in_7), .clk(clock_1_out), .K(in_7), .Q(out_15), .Qn(j_k_ff_1_qn), .reset(and_3_out));  // open: preset, en
  xor xor_1 (xor_1_out, A, B);
  and and_1 (and_1_out, B, A);
  J_K_Flip_Flop j_k_ff_2 (
    .J(in_7), .clk(j_k_ff_1_qn), .K(in_7), .Q(out_14), .Qn(j_k_ff_2_qn), .reset(and_3_out));  // open: preset, en
  xor xor_2 (Sum, xor_1_out, C);
  and and_2 (and_2_out, C, xor_1_out);
  or or_1 (Carry_2, and_2_out, and_1_out);
  J_K_Flip_Flop j_k_ff_3 (
    .J(in_7), .clk(j_k_ff_2_qn), .K(in_7), .Q(out_13), .Qn(j_k_ff_3_qn), .reset(and_3_out));  // open: preset, en
  and and_3 (and_3_out, out_12, out_13, out_15);
  J_K_Flip_Flop j_k_ff_4 (
    .J(in_7), .clk(j_k_ff_3_qn), .K(in_7), .Q(out_12), .reset(and_3_out));  // open: Qn, preset, en
  Adder #(.width(1)) adder_1 (.a(A_2), .b(B_2), .out(Sum_2), .cin(C_2), .cout(Carry));

  // Notes on the sheet:
  //   Number 2
  //   Number !
  //   Mod 13 Counter
endmodule
