// Logisim project Mod60.circ as structural Verilog: 1 circuit, main circuit main
module main (
  input  in_1,
  input  in_2,
  output out_3,
  output out_4,
  output out_5,
  output out_6,
  output out_7,
  output out_8,
  output out_9,
  output out_10
);

  wire and_1_out, and_2_out, and_3_out, clock_1_out, j_k_ff_1_qn, j_k_ff_2_qn, j_k_ff_3_qn, j_k_ff_6_qn,
       j_k_ff_7_qn;

  Clock clock_1 (.out(clock_1_out));
  and and_1 (and_1_out, out_5, out_3);
  J_K_Flip_Flop j_k_ff_1 (
    .J(in_1), .clk(clock_1_out), .K(in_1), .Q(out_6), .Qn(j_k_ff_1_qn), .reset(and_1_out));  // open: preset, en
  and and_2 (and_2_out, out_3, out_5);
  J_K_Flip_Flop j_k_ff_2 (
    .J(in_1), .clk(j_k_ff_1_qn), .K(in_1), .Q(out_5), .Qn(j_k_ff_2_qn), .reset(and_1_out));  // open: preset, en
  J_K_Flip_Flop j_k_ff_3 (
    .J(in_1), .clk(j_k_ff_2_qn), .K(in_1), .Q(out_4), .Qn(j_k_ff_3_qn), .reset(and_1_out));  // open: preset, en
  J_K_Flip_Flop j_k_ff_4 (.J(in_1), .clk(j_k_ff_3_qn), .K(in_1), .Q(out_3), .reset(and_1_out));  // open: Qn, preset, en
  J_K_Flip_Flop j_k_ff_5 (.J(in_2), .K(in_2), .Q(out_10), .reset(and_3_out));  // open: clk, Qn, preset, en
  and and_3 (and_3_out, out_8, out_7);
  J_K_Flip_Flop j_k_ff_6 (
    .J(in_2), .clk(and_2_out), .K(in_2), .Q(out_9), .Qn(j_k_ff_6_qn), .reset(and_3_out));  // open: preset, en
  J_K_Flip_Flop j_k_ff_7 (
    .J(in_2), .clk(j_k_ff_6_qn), .K(in_2), .Q(out_8), .Qn(j_k_ff_7_qn), .reset(and_3_out));  // open: preset, en
  J_K_Flip_Flop j_k_ff_8 (.J(in_2), .clk(j_k_ff_7_qn), .K(in_2), .Q(out_7), .reset(and_3_out));  // open: Qn, preset, en
endmodule
