// Logisim project PIPO.circ as structural Verilog: 1 circuit, main circuit main
module main (
  input  in_1,
  input  in_2,
  input  in_3,
  input  in_4,
  input  D5,
  input  D4,
  input  D3,
  input  D2,
  input  D1,
  input  D0,
  output out_11,
  output out_12,
  output out_13,
  output out_14,
  output Q5,
  output Q4,
  output Q3,
  output Q2,
  output Q1,
  output Q0
);

  wire Clk_out, Cp_out, MR_out, Reset_out;

  Clock Clk (.out(Clk_out));
  Button Reset (.out(Reset_out));
  Button MR (.out(MR_out));
  Clock Cp (.out(Cp_out));
  D_Flip_Flop d_ff_1 (.clk(Clk_out), .D(in_1), .Q(out_11), .reset(Reset_out));  // open: Qn, preset, en
  D_Flip_Flop d_ff_2 (.clk(Cp_out), .D(D5), .Q(Q5), .reset(MR_out));  // open: Qn, preset, en
  D_Flip_Flop d_ff_3 (.clk(Clk_out), .D(in_2), .Q(out_12), .reset(Reset_out));  // open: Qn, preset, en
  D_Flip_Flop d_ff_4 (.clk(Cp_out), .D(D4), .Q(Q4), .reset(MR_out));  // open: Qn, preset, en
  D_Flip_Flop d_ff_5 (.clk(Clk_out), .D(in_3), .Q(out_13), .reset(Reset_out));  // open: Qn, preset, en
  D_Flip_Flop d_ff_6 (.clk(Cp_out), .D(D3), .Q(Q3), .reset(MR_out));  // open: Qn, preset, en
  D_Flip_Flop d_ff_7 (.clk(Clk_out), .D(in_4), .Q(out_14), .reset(Reset_out));  // open: Qn, preset, en
  D_Flip_Flop d_ff_8 (.clk(Cp_out), .D(D2), .Q(Q2), .reset(MR_out));  // open: Qn, preset, en
  D_Flip_Flop d_ff_9 (.clk(Cp_out), .D(D1), .Q(Q1), .reset(MR_out));  // open: Qn, preset, en
  D_Flip_Flop d_ff_10 (.clk(Cp_out), .D(D0), .Q(Q0), .reset(MR_out));  // open: Qn, preset, en

  // Notes on the sheet:
  //   IN
  //                               PIPO = Parallel in, Paraller out
  //   OUT
  //   74ALS174
endmodule
