// Logisim project Shift Resistor.circ as structural Verilog: 1 circuit, main circuit main
module main (
  input  in_1,
  input  in_2,
  output out_3,
  output out_4
);

  wire clock_1_out, clock_2_out, d_ff_1_q, d_ff_2_q, d_ff_3_q, d_ff_4_q, d_ff_5_q, d_ff_6_q, Reset_2_out,
       Reset_out;

  Clock clock_1 (.out(clock_1_out));
  Button Reset (.out(Reset_out));
  Clock clock_2 (.out(clock_2_out));
  Button Reset_2 (.out(Reset_2_out));
  D_Flip_Flop d_ff_1 (.clk(clock_1_out), .D(out_3), .Q(d_ff_1_q), .reset(Reset_out));  // open: Qn, preset, en
  D_Flip_Flop d_ff_2 (.clk(clock_2_out), .D(out_4), .Q(d_ff_2_q), .reset(Reset_2_out));  // open: Qn, preset, en
  D_Flip_Flop d_ff_3 (.clk(clock_1_out), .D(d_ff_1_q), .Q(d_ff_3_q), .reset(Reset_out));  // open: Qn, preset, en
  D_Flip_Flop d_ff_4 (.clk(clock_2_out), .D(d_ff_2_q), .Q(d_ff_4_q), .reset(Reset_2_out));  // open: Qn, preset, en
  D_Flip_Flop d_ff_5 (.clk(clock_1_out), .D(d_ff_3_q), .Q(d_ff_5_q), .reset(Reset_out));  // open: Qn, preset, en
  D_Flip_Flop d_ff_6 (.clk(clock_2_out), .D(d_ff_4_q), .Q(d_ff_6_q), .reset(Reset_2_out));  // open: Qn, preset, en
  D_Flip_Flop d_ff_7 (.clk(clock_1_out), .D(d_ff_5_q), .Q(out_3), .reset(Reset_out));  // open: Qn, preset, en
  D_Flip_Flop d_ff_8 (.clk(clock_2_out), .D(d_ff_6_q), .Qn(out_4), .reset(Reset_2_out));  // open: Q, preset, en

  // Notes on the sheet:
  //   Ring Counter
  //   Johnson or Twisted Ring Counter
endmodule
