// Logisim project SR and D FlipFlop.circ as structural Verilog: 1 circuit, main circuit main
module main (
  input  in_1,
  input  in_2,
  input  in_3,
  output out_4,
  output out_5,
  output out_6,
  output out_7
);

  wire not_1_out;

  not not_1 (not_1_out, in_3);
  nand nand_1 (out_4, in_1, out_5);
  nand nand_2 (out_5, out_4, in_2);
  nand nand_3 (out_6, in_3, out_7);
  nand nand_4 (out_7, out_6, not_1_out);
endmodule
