// Logisim project Basic Gate.circ as structural Verilog: 1 circuit, main circuit main
module main (
  input  Vdd,
  input  Vdd_2,
  input  Vdd_3,
  input  A,
  input  A_2,
  input  A_3,
  input  B,
  input  B_2,
  input  Vdd_4,
  input  Vdd_5,
  input  A_4,
  input  A_5,
  input  B_3,
  input  B_4,
  output Out,
  output Out_2,
  output Out_3,
  output Out_4,
  output Out_5
);

  wire transistor_2_out, transistor_3_out, transistor_4_out, transistor_5_out, transistor_7_out,
       transistor_8_out, transistor_13_out, transistor_14_out, transistor_15_out, transistor_18_out,
       transistor_19_out;

  Transistor transistor_1 (.in(Vdd), .out(Out), .gate(A_3));
  Transistor #(.\type ("n")) transistor_2 (.in(Out), .out(transistor_2_out), .gate(A_3));
  Transistor #(.\type ("n")) transistor_3 (.in(transistor_5_out), .out(transistor_3_out), .gate(A_4));
  Transistor transistor_4 (.in(Vdd_4), .out(transistor_4_out), .gate(A_4));
  Transistor transistor_5 (.in(transistor_4_out), .out(transistor_5_out), .gate(B_3));
  Transistor #(.\type ("n")) transistor_6 (.in(transistor_5_out), .out(transistor_3_out), .gate(B_3));
  Transistor #(.\type ("n")) transistor_7 (.in(Out_2), .out(transistor_7_out), .gate(A));
  Transistor transistor_8 (.in(Vdd_2), .out(transistor_8_out), .gate(A));
  Transistor transistor_9 (.in(transistor_8_out), .out(Out_2), .gate(B));
  Transistor transistor_10 (.in(Vdd_4), .out(Out_4), .gate(transistor_5_out));
  Transistor #(.\type ("n")) transistor_11 (.in(Out_4), .out(transistor_3_out), .gate(transistor_5_out));
  Transistor #(.\type ("n")) transistor_12 (.in(Out_2), .out(transistor_7_out), .gate(B));
  Transistor transistor_13 (.in(Vdd_5), .out(transistor_13_out), .gate(A_5));
  Transistor #(.\type ("n")) transistor_14 (.in(transistor_13_out), .out(transistor_14_out), .gate(A_5));
  Transistor #(.\type ("n")) transistor_15 (.in(transistor_14_out), .out(transistor_15_out), .gate(B_4));
  Transistor transistor_16 (.in(Vdd_3), .out(Out_3), .gate(A_2));
  Transistor transistor_17 (.in(Vdd_5), .out(transistor_13_out), .gate(B_4));
  Transistor #(.\type ("n")) transistor_18 (.in(Out_3), .out(transistor_18_out), .gate(A_2));
  Transistor #(.\type ("n")) transistor_19 (.in(transistor_18_out), .out(transistor_19_out), .gate(B_2));
  Transistor transistor_20 (.in(Vdd_3), .out(Out_3), .gate(B_2));
  Transistor transistor_21 (.in(Vdd_5), .out(Out_5), .gate(transistor_13_out));
  Transistor #(.\type ("n")) transistor_22 (.in(Out_5), .out(transistor_15_out), .gate(transistor_13_out));
  // also tied to GND on the sheet: {transistor_2_out, transistor_3_out, transistor_7_out, transistor_15_out, transistor_19_out}

  // Notes on the sheet:
  //   G
  //   G
  //   Not Gate
  //   S
  //   D
  //   D
  //   S
  //   Or Gate
  //   G
  //   G
  //   D
  //   G
  //   S
  //   S
  //   D
  //   S
  //   D
  //   G
  //   D
  //   S
  //   G
  //   G
  //   D
  //   G
  //   S
  //   Nor Gate
  //   G
  //   G
  //   S
  //   D
  //   S
  //   D
  //   G
  //   S
  //   D
  //   D
  //   S
  //   D
  //   S
  //   S
  //   D
  //   And Gate
  //   Nand Gate
  //   D
  //   S
  //   D
  //   S
  //   S
  //   D
  //   S
  //   D
  //   D
  //   S
  //   D
  //   S
  //   S
  //   D
  //   S
  //   G
  //   D
  //   D
  //   G
  //   S
endmodule
