// Logisim project Universal Gate 1.circ as structural Verilog: 1 circuit, main circuit main
module main (
  input  A,
  input  B,
  output F_A_prime,
  output F_A_B,
  output F_A_B_2,
  output out_6,
  output out_7,
  output F_A_B_3
);

  wire nand_2_out, nand_3_out, nand_4_out, nor_2_out, nor_3_out, nor_4_out;

  nand nand_1 (F_A_prime, A, A);
  nand nand_2 (nand_2_out, A, B);
  nand nand_3 (nand_3_out, A, A);
  nand nand_4 (nand_4_out, B, B);
  nor nor_1 (out_6, A, A);
  nor nor_2 (nor_2_out, A, A);
  nor nor_3 (nor_3_out, B, B);
  nor nor_4 (nor_4_out, A, B);
  nand nand_5 (F_A_B, nand_2_out, nand_2_out);
  nand nand_6 (F_A_B_2, nand_3_out, nand_4_out);
  nor nor_5 (out_7, nor_2_out, nor_3_out);
  nor nor_6 (F_A_B_3, nor_4_out, nor_4_out);

  // Notes on the sheet:
  //   NOR Gate Applications
  //   NAND Gate Applications
  //   F=A'
  //   F=A.B
  //   NOT Gate
  //   AND Gate
  //   OR Gate
  //   NOT Gate
  //   AND Gate
  //   OR Gate
endmodule
