// Logisim project Universal Gate 2.circ as structural Verilog: 1 circuit, main circuit main
module main (
  input  A,
  input  B,
  output out_3,
  output F_AB_prime___A_prime_B
);

  wire nand_1_out, nand_2_out, nand_3_out, nand_4_out, nor_1_out, nor_2_out, nor_3_out, nor_4_out;

  nand nand_1 (nand_1_out, A, A);
  nand nand_2 (nand_2_out, B, B);
  nor nor_1 (nor_1_out, A, A);
  nor nor_2 (nor_2_out, B, B);
  nor nor_3 (nor_3_out, A, B);
  nand nand_3 (nand_3_out, nand_1_out, B);
  nand nand_4 (nand_4_out, A, nand_2_out);
  nor nor_4 (nor_4_out, nor_1_out, nor_2_out);
  nand nand_5 (out_3, nand_3_out, nand_4_out);
  nor nor_5 (F_AB_prime___A_prime_B, nor_4_out, nor_3_out);

  // Notes on the sheet:
  //   Using NAND Gate
  //   Using NOR Gate
  //   Construction of X-OR Gate
  //   F=AB' + A'B
endmodule
