// Logisim project Universal Gate 3.circ as structural Verilog: 1 circuit, main circuit main
module main (
  input  A,
  input  B,
  output out_3,
  output out_4
);

  wire nand_1_out, nand_2_out, nand_3_out, nand_4_out, nor_1_out, nor_2_out, nor_3_out;

  nand nand_1 (nand_1_out, A, B);
  nor nor_1 (nor_1_out, A, B);
  nand nand_2 (nand_2_out, A, nand_1_out);
  nand nand_3 (nand_3_out, nand_1_out, B);
  nor nor_2 (nor_2_out, A, nor_1_out);
  nor nor_3 (nor_3_out, nor_1_out, B);
  nand nand_4 (nand_4_out, nand_2_out, nand_3_out);
  nor nor_4 (out_4, nor_2_out, nor_3_out);
  nand nand_5 (out_3, nand_4_out, nand_4_out);

  // Notes on the sheet:
  //   Using NOR Gate
  //   Construction of X-NOR Gate
  //   Using NAND Gate
  //   F = (AB' + A'B)'
  //   F = (AB' + A'B)'
endmodule
