// Logisim project assignment2.circ as structural Verilog: 1 circuit, main circuit main
module main (
  output Q1,
  output Q2
);

  wire Clk_out, d_ff_1_qn, J_out, K_out;

  Clock J (.out(J_out));
  Clock K (.out(K_out));
  Clock Clk (.out(Clk_out));
  J_K_Flip_Flop j_k_ff_1 (.J(J_out), .clk(Clk_out), .K(K_out), .Q(Q1));  // open: Qn, preset, en, reset
  D_Flip_Flop d_ff_1 (.clk(Q1), .D(d_ff_1_qn), .Q(Q2), .Qn(d_ff_1_qn));  // open: preset, en, reset
endmodule
