// Logisim project test.circ as structural Verilog: 1 circuit, main circuit main
module main (
  input  in_1,
  input  in_2,
  input  in_3,
  input  in_4,
  output out_5,
  output out_6,
  output out_7,
  output out_8,
  output out_9,
  output out_10
);

  wire clock_1_out, d_ff_1_qn, d_ff_2_qn, not_1_out;

  Clock clock_1 (.out(clock_1_out));
  not not_1 (not_1_out, clock_1_out);
  J_K_Flip_Flop j_k_ff_1 (.J(in_2), .clk(not_1_out), .K(in_2), .Q(out_10));  // open: Qn, preset, en, reset
  J_K_Flip_Flop j_k_ff_2 (.J(in_1), .clk(not_1_out), .K(in_1), .Q(out_5));  // open: Qn, preset, en, reset
  D_Flip_Flop d_ff_1 (.clk(not_1_out), .D(d_ff_1_qn), .Q(out_6), .Qn(d_ff_1_qn));  // open: preset, en, reset
  J_K_Flip_Flop j_k_ff_3 (.J(in_2), .clk(out_10), .K(in_2), .Q(out_9));  // open: Qn, preset, en, reset
  J_K_Flip_Flop j_k_ff_4 (.J(in_3), .clk(not_1_out), .K(in_4), .Q(out_8));  // open: Qn, preset, en, reset
  D_Flip_Flop d_ff_2 (.clk(out_8), .D(d_ff_2_qn), .Q(out_7), .Qn(d_ff_2_qn));  // open: preset, en, reset

  // Notes on the sheet:
  //   Normal 2 bit Down Counter
  //   Both the flip flop equavalent
  //   Assignment
endmodule
